// Logisim project alu.circ as structural Verilog
module ALU (
  input  [31:0] X,
  input  [31:0] Y,
  input  [3:0] AluOP,
  output Signed_Overflow,
  output UnSigned_Overflow,
  output Equal,
  output [31:0] Result,
  output [31:0] Result_2
);

  wire and_1_out, C, FF, or_2_out, or_3_out, S5, S6, xnor_1_out, xor_1_out, xor_2_out, YY;
  wire [0:0] comparator_3_lt, comparator_4_lt;
  wire [30:0] multiplexer_1_out, n32bitadder_1_f;
  wire [31:0] and_2_out, divider_1_out, divider_1_rem, multiplier_1_cout, multiplier_1_out, nor_1_out,
       not_1_out, or_1_out, shifter_1_out, shifter_2_out, shifter_3_out, xor_3_out;

  // Probe on X
  // Probe on X
  Comparator #(.width(4), .mode("unsigned")) comparator_1 (.a(4'b0110), .b(AluOP), .eq(S6));  // open: gt, lt
  // Probe on Y
  // Probe on Y
  Multiplexer #(.width(32), .enable("false")) multiplexer_1 (
    .in0(Y), .in1(not_1_out), .out({YY, multiplexer_1_out}), .sel(S6));
  assign not_1_out = ~Y;  // NOT_Gate not_1, 32 bits wide
  Comparator #(.width(4), .mode("unsigned")) comparator_2 (.a(4'b0101), .b(AluOP), .eq(S5));  // open: gt, lt
  xnor xnor_1 (xnor_1_out, YY, X[31]);
  xor xor_1 (xor_1_out, X[31], FF);
  // Probe on AluOP
  and and_1 (and_1_out, xnor_1_out, xor_1_out);
  xor xor_2 (xor_2_out, S6, C);
  // Probe on Result
  // Probe on Result
  Shifter #(.width(32)) shifter_1 (.in(X), .\dist (Y[4:0]), .out(shifter_1_out));
  Shifter #(.width(32), .shift("ar")) shifter_2 (.in(X), .\dist (Y[4:0]), .out(shifter_2_out));
  Shifter #(.width(32), .shift("lr")) shifter_3 (.in(X), .\dist (Y[4:0]), .out(shifter_3_out));
  Multiplier #(.width(32)) multiplier_1 (.a(X), .b(Y), .out(multiplier_1_out), .cout(multiplier_1_cout));  // open: cin
  Divider #(.width(32)) divider_1 (.a(X), .b(Y), .out(divider_1_out), .rem(divider_1_rem));  // open: upper
  _32bitadder u_32bitadder_1 (.in_1(X), .in_2({YY, multiplexer_1_out}), .C0(S6), .F({FF, n32bitadder_1_f}), .out_5(C));
  assign and_2_out = X & Y;  // AND_Gate and_2, 32 bits wide
  assign or_1_out = X | Y;  // OR_Gate or_1, 32 bits wide
  Comparator #(.width(32)) comparator_3 (.a(X), .b(Y), .eq(Equal), .lt(comparator_3_lt[0]));  // open: gt
  Comparator #(.width(32), .mode("unsigned")) comparator_4 (.a(X), .b(Y), .lt(comparator_4_lt[0]));  // open: gt, eq
  or or_2 (or_2_out, S5, S6);
  Multiplexer #(.enable("false")) multiplexer_2 (.in0(1'b0), .in1(and_1_out), .out(Signed_Overflow), .sel(or_2_out));
  or or_3 (or_3_out, S5, S6);
  Multiplexer #(.enable("false")) multiplexer_3 (.in0(1'b0), .in1(xor_2_out), .out(UnSigned_Overflow), .sel(or_3_out));
  assign xor_3_out = X ^ Y;  // XOR_Gate xor_3, 32 bits wide
  assign nor_1_out = ~(X | Y);  // NOR_Gate nor_1, 32 bits wide
  // Probe on Result_2
  Multiplexer #(.select(4), .width(32), .enable("false")) multiplexer_4 (
    .in0(shifter_1_out), .in1(shifter_2_out), .in2(shifter_3_out), .in3(multiplier_1_out),
    .in4(divider_1_out), .in5({FF, n32bitadder_1_f}), .in6({FF, n32bitadder_1_f}), .in7(and_2_out),
    .in8(or_1_out), .in9(xor_3_out), .in10(nor_1_out), .in11({{31{1'b0}}, comparator_3_lt[0]}),
    .in12({{31{1'b0}}, comparator_4_lt[0]}), .in13({32{1'b0}}), .in14({32{1'b0}}), .in15({32{1'b0}}),
    .out(Result), .sel(AluOP));
  Multiplexer #(.select(4), .width(32), .enable("false")) multiplexer_5 (
    .in0({32{1'b0}}), .in1({32{1'b0}}), .in2({32{1'b0}}), .in3(multiplier_1_cout), .in4(divider_1_rem),
    .in5({32{1'b0}}), .in6({32{1'b0}}), .in7({32{1'b0}}), .in8({32{1'b0}}), .in9({32{1'b0}}),
    .in10({32{1'b0}}), .in11({32{1'b0}}), .in12({32{1'b0}}), .in13({32{1'b0}}), .in14({32{1'b0}}),
    .in15({32{1'b0}}), .out(Result_2), .sel(AluOP));

  // Other names for the same wires on the sheet: OF = Signed_Overflow; Result2[31:0] = Result_2; S[3:0] = AluOP;
  //   UOF = UnSigned_Overflow; XX = X[31]

  // Notes on the sheet:
  //   不要改变此引脚区域内容，也不要改变ALU封装形式
  //   输入引脚
  //   请在下方利用上方输入输出引脚的隧道信号构建ALU电路，ctrl+d复制选择部件
  //   华中科技大学计算机学院 计算机组成原理，鸣谢加州大学伯克利CS61C课程
  //   输出引脚
  //   探测区域
endmodule

module \演示电路  (
  input  [31:0] X,
  input  [31:0] Y,
  input  [3:0] ALUOP,
  output Signed_Overflow,
  output Unsigned_overflow,
  output [31:0] Result,
  output [31:0] Result_2,
  output Equal
);

  // Probe on X
  // Probe on X
  ALU alu_1 (
    .AluOP(ALUOP), .X(X), .Equal(Equal), .Result(Result), .Signed_Overflow(Signed_Overflow), .Y(Y),
    .Result_2(Result_2), .UnSigned_Overflow(Unsigned_overflow));
  // Probe on ALUOP
  // Probe on Y
  // Probe on Y
  // Probe on Result
  // Probe on Result
  // Probe on Result_2

  // Notes on the sheet:
  //   ALu电路无需调整位置即可连接在该电路中，并且不能出现蓝色线缆和三态输出
endmodule

module \等差数列  (
  input  [31:0] \数列初始值 ,
  input  [31:0] \等差值 ,
  input  \时钟 ,
  output [31:0] Result
);

  // Probe on \数列初始值 
  // Probe on \数列初始值 
  // Probe on \等差值 
  // Probe on \等差值 
  // Probe on Result
  // Probe on Result

  // Other names for the same wires on the sheet: 数列初值[31:0] = \数列初始值 ; 累加和[31:0] = Result

  // Notes on the sheet:
  //   不要改变此引脚区域内容，也不要改变ALU封装形式
  //   请在下方利用上方输入输出引脚的隧道信号构建等差数列求和电路，ctrl+d复制选择部件
  //   华中科技大学计算机学院 计算机组成原理，鸣谢加州大学伯克利CS61C课程
  //   输出引脚
  //   探测区域
endmodule

module _74182 (
  input  Cn,
  input  P3,
  input  G3,
  input  P2,
  input  G2,
  input  P1,
  input  G1,
  input  P0,
  input  G0,
  output Cz,
  output Cy,
  output P,
  output G,
  output Cx
);

  wire and_1_out, and_2_out, and_3_out, and_4_out, and_5_out, and_6_out, and_7_out, and_8_out, and_9_out,
       and_10_out, and_11_out, and_12_out, and_13_out, not_2_out, not_3_out, not_4_out, not_5_out, not_6_out,
       not_7_out, not_8_out, not_9_out, not_10_out, or_1_out;

  not not_1 (P, or_1_out);
  or or_1 (or_1_out, not_2_out, not_4_out, not_6_out, not_8_out);
  and and_1 (and_1_out, not_9_out, not_7_out, not_5_out, not_3_out);
  nor nor_1 (G, and_1_out, and_2_out, and_3_out, and_4_out);
  and and_2 (and_2_out, not_6_out, not_7_out, not_5_out, not_3_out);
  and and_3 (and_3_out, not_4_out, not_5_out, not_3_out);
  not not_2 (not_2_out, P3);
  and and_4 (and_4_out, not_2_out, not_3_out);
  not not_3 (not_3_out, G3);
  and and_5 (and_5_out, not_5_out, not_7_out, not_9_out, not_8_out);
  and and_6 (and_6_out, not_5_out, not_7_out, not_9_out, not_10_out);
  nor nor_2 (Cz, and_6_out, and_5_out, and_7_out, and_8_out);
  and and_7 (and_7_out, not_5_out, not_7_out, not_6_out);
  and and_8 (and_8_out, not_4_out, not_5_out);
  not not_4 (not_4_out, P2);
  not not_5 (not_5_out, G2);
  and and_9 (and_9_out, not_9_out, not_7_out, not_10_out);
  nor nor_3 (Cy, and_9_out, and_10_out, and_11_out);
  and and_10 (and_10_out, not_8_out, not_9_out, not_7_out);
  and and_11 (and_11_out, not_6_out, not_7_out);
  not not_6 (not_6_out, P1);
  not not_7 (not_7_out, G1);
  nor nor_4 (Cx, and_13_out, and_12_out);
  and and_12 (and_12_out, not_8_out, not_9_out);
  and and_13 (and_13_out, not_9_out, not_10_out);
  not not_8 (not_8_out, P0);
  not not_9 (not_9_out, G0);
  not not_10 (not_10_out, Cn);
endmodule

module adder (
  input  A,
  input  B,
  input  C0,
  output F,
  output C1
);

  wire and_1_out, and_2_out, xor_1_out;

  xor xor_1 (xor_1_out, A, B);
  and and_1 (and_1_out, A, B);
  xor xor_2 (F, xor_1_out, C0);
  and and_2 (and_2_out, C0, xor_1_out);
  or or_1 (C1, and_2_out, and_1_out);
endmodule

module _4bitadder (
  input  [3:0] A,
  input  [3:0] B,
  input  C0,
  output [3:0] out,
  output out_5,
  output out_6,
  output out_7
);

  wire and_1_out, and_2_out, and_3_out, and_4_out, and_5_out, and_6_out, and_7_out, and_8_out, and_9_out,
       and_10_out, and_11_out, and_12_out, and_13_out, and_14_out, and_15_out, and_16_out, and_17_out,
       and_18_out, and_19_out, and_21_out, C1, C2, C3, or_1_out, or_2_out, or_3_out, or_4_out, or_5_out,
       or_6_out, or_10_out, or_11_out, or_12_out, or_13_out;

  adder adder_1 (.A(A[0]), .B(B[0]), .C0(C0), .F(out[0]));  // open: C1
  adder adder_2 (.A(A[1]), .B(B[1]), .C0(C1), .F(out[1]));  // open: C1
  adder adder_3 (.A(A[2]), .B(B[2]), .C0(C2), .F(out[2]));  // open: C1
  adder adder_4 (.A(A[3]), .B(B[3]), .C0(C3), .F(out[3]));  // open: C1
  and and_1 (and_1_out, A[0], B[0]);
  or or_1 (or_1_out, A[0], B[0]);
  or or_2 (or_2_out, A[1], B[1]);
  and and_2 (and_2_out, A[0], B[0]);
  or or_3 (or_3_out, A[0], B[0]);
  or or_4 (or_4_out, A[2], B[2]);
  and and_3 (and_3_out, A[1], B[1]);
  or or_5 (or_5_out, A[1], B[1]);
  and and_4 (and_4_out, A[0], B[0]);
  or or_6 (or_6_out, A[0], B[0]);
  and and_5 (and_5_out, or_1_out, C0);
  and and_6 (and_6_out, A[1], B[1]);
  and and_7 (and_7_out, or_2_out, and_2_out);
  and and_8 (and_8_out, or_2_out, or_3_out, C0);
  and and_9 (and_9_out, A[2], B[2]);
  and and_10 (and_10_out, or_4_out, and_3_out);
  and and_11 (and_11_out, or_4_out, or_5_out, and_4_out);
  and and_12 (and_12_out, or_4_out, or_5_out, or_6_out, C0);
  or or_7 (C1, and_1_out, and_5_out);
  or or_8 (C2, and_6_out, and_7_out, and_8_out);
  or or_9 (C3, and_9_out, and_10_out, and_11_out, and_12_out);
  or or_10 (or_10_out, A[3], B[3]);
  and and_13 (and_13_out, A[2], B[2]);
  or or_11 (or_11_out, A[2], B[2]);
  and and_14 (and_14_out, A[1], B[1]);
  or or_12 (or_12_out, A[1], B[1]);
  and and_15 (and_15_out, A[0], B[0]);
  or or_13 (or_13_out, A[0], B[0]);
  and and_16 (and_16_out, A[3], B[3]);
  and and_17 (and_17_out, or_10_out, and_13_out);
  and and_18 (and_18_out, or_10_out, or_11_out, and_14_out);
  and and_19 (and_19_out, or_10_out, or_11_out, or_12_out, and_15_out);
  and and_20 (out_6, or_10_out, or_11_out, or_12_out, or_13_out);
  or or_14 (out_7, and_16_out, and_17_out, and_18_out, and_19_out);
  and and_21 (and_21_out, out_6, C0);
  or or_15 (out_5, out_7, and_21_out);

  // Other names for the same wires on the sheet: C4 = out_5; G = out_7; P = out_6
endmodule

// Adder
module _32bitadder (
  input  [31:0] in_1,
  input  [31:0] in_2,
  input  C0,
  output [31:0] F,
  output out_5
);

  wire C1, C2, C3, C4, C5, C6, C7, n4bitadder_1_out_6, n4bitadder_1_out_7, n4bitadder_2_out_6,
       n4bitadder_2_out_7, n4bitadder_3_out_6, n4bitadder_3_out_7, n4bitadder_4_out_6, n4bitadder_4_out_7,
       n4bitadder_5_out_6, n4bitadder_5_out_7, n4bitadder_6_out_6, n4bitadder_6_out_7, n4bitadder_7_out_6,
       n4bitadder_7_out_7, n4bitadder_8_out_6, n4bitadder_8_out_7, n74182_3_g, n74182_3_p;

  // Probe on in_1
  // Probe on in_2
  // Probe on F
  _4bitadder u_4bitadder_1 (
    .A(in_1[31:28]), .B(in_2[31:28]), .C0(C7), .out(F[31:28]), .out_5(out_5), .out_6(n4bitadder_1_out_6),
    .out_7(n4bitadder_1_out_7));
  _4bitadder u_4bitadder_2 (
    .A(in_1[27:24]), .B(in_2[27:24]), .C0(C6), .out(F[27:24]), .out_6(n4bitadder_2_out_6),
    .out_7(n4bitadder_2_out_7));  // open: out_5
  _74182 u_74182_1 (
    .Cn(C4), .Cz(C7), .Cy(C6), .Cx(C5), .P3(n4bitadder_1_out_6), .G3(n4bitadder_1_out_7),
    .P2(n4bitadder_2_out_6), .G2(n4bitadder_2_out_7), .P1(n4bitadder_3_out_6), .G1(n4bitadder_3_out_7),
    .P0(n4bitadder_4_out_6), .G0(n4bitadder_4_out_7));  // open: P, G
  _4bitadder u_4bitadder_3 (
    .A(in_1[23:20]), .B(in_2[23:20]), .C0(C5), .out(F[23:20]), .out_6(n4bitadder_3_out_6),
    .out_7(n4bitadder_3_out_7));  // open: out_5
  _74182 u_74182_2 (.Cn(C0), .Cx(C4), .P0(n74182_3_p), .G0(n74182_3_g));  // open: P, G, Cz, Cy, P3, G3, P2, G2, P1, G1
  _4bitadder u_4bitadder_4 (
    .A(in_1[19:16]), .B(in_2[19:16]), .C0(C4), .out(F[19:16]), .out_6(n4bitadder_4_out_6),
    .out_7(n4bitadder_4_out_7));  // open: out_5
  _4bitadder u_4bitadder_5 (
    .A(in_1[15:12]), .B(in_2[15:12]), .C0(C3), .out(F[15:12]), .out_6(n4bitadder_5_out_6),
    .out_7(n4bitadder_5_out_7));  // open: out_5
  _4bitadder u_4bitadder_6 (
    .A(in_1[11:8]), .B(in_2[11:8]), .C0(C2), .out(F[11:8]), .out_6(n4bitadder_6_out_6),
    .out_7(n4bitadder_6_out_7));  // open: out_5
  _74182 u_74182_3 (
    .Cn(C0), .P(n74182_3_p), .G(n74182_3_g), .Cz(C3), .Cy(C2), .Cx(C1), .P3(n4bitadder_5_out_6),
    .G3(n4bitadder_5_out_7), .P2(n4bitadder_6_out_6), .G2(n4bitadder_6_out_7), .P1(n4bitadder_7_out_6),
    .G1(n4bitadder_7_out_7), .P0(n4bitadder_8_out_6), .G0(n4bitadder_8_out_7));
  _4bitadder u_4bitadder_7 (
    .A(in_1[7:4]), .B(in_2[7:4]), .C0(C1), .out(F[7:4]), .out_6(n4bitadder_7_out_6),
    .out_7(n4bitadder_7_out_7));  // open: out_5
  _4bitadder u_4bitadder_8 (
    .A(in_1[3:0]), .B(in_2[3:0]), .C0(C0), .out(F[3:0]), .out_6(n4bitadder_8_out_6),
    .out_7(n4bitadder_8_out_7));  // open: out_5

  // Other names for the same wires on the sheet: C8 = out_5; F0[3:0] = F[3:0]; F1[3:0] = F[7:4]; F2[3:0] = F[11:8];
  //   F3[3:0] = F[15:12]; F4[3:0] = F[19:16]; F5[3:0] = F[23:20]; F6[3:0] = F[27:24]; F7[3:0] = F[31:28];
  //   A0[3:0] = in_1[3:0]; A1[3:0] = in_1[7:4]; A2[3:0] = in_1[11:8]; A3[3:0] = in_1[15:12]; A4[3:0] = in_1[19:16];
  //   A5[3:0] = in_1[23:20]; A6[3:0] = in_1[27:24]; A7[3:0] = in_1[31:28]; B0[3:0] = in_2[3:0]; B1[3:0] = in_2[7:4];
  //   B2[3:0] = in_2[11:8]; B3[3:0] = in_2[15:12]; B4[3:0] = in_2[19:16]; B5[3:0] = in_2[23:20];
  //   B6[3:0] = in_2[27:24]; B7[3:0] = in_2[31:28]

  // Notes on the sheet:
  //   A
  //   B
endmodule

module test (
  input  [31:0] X,
  input  [31:0] Y,
  input  [3:0] AluOP,
  input  in_4,
  output Signed_Overflow,
  output UnSigned_Overflow,
  output Equal,
  output [31:0] Result,
  output [31:0] Result_2,
  output out,
  output out_2,
  output out_3
);

  wire and_1_out, C, FF, n32bitadder_2_out_5, or_2_out, or_3_out, S5, S6, xnor_1_out, xor_1_out, xor_2_out,
       YY;
  wire [0:0] comparator_3_lt, comparator_4_lt;
  wire [30:0] multiplexer_1_out, n32bitadder_1_f;
  wire [31:0] and_2_out, divider_1_out, divider_1_rem, multiplexer_6_out, multiplier_1_cout,
       multiplier_1_out, n32bitadder_2_f, nor_1_out, not_1_out, not_2_out, or_1_out, shifter_1_out,
       shifter_2_out, shifter_3_out, xor_3_out;

  // Probe on X
  // Probe on X
  Comparator #(.width(4), .mode("unsigned")) comparator_1 (.a(4'b0110), .b(AluOP), .eq(S6));  // open: gt, lt
  // Probe on Y
  // Probe on Y
  Multiplexer #(.width(32), .enable("false")) multiplexer_1 (
    .in0(Y), .in1(not_1_out), .out({YY, multiplexer_1_out}), .sel(S6));
  assign not_1_out = ~Y;  // NOT_Gate not_1, 32 bits wide
  Comparator #(.width(4), .mode("unsigned")) comparator_2 (.a(4'b0101), .b(AluOP), .eq(S5));  // open: gt, lt
  xnor xnor_1 (xnor_1_out, YY, X[31]);
  xor xor_1 (xor_1_out, X[31], FF);
  // Probe on AluOP
  and and_1 (and_1_out, xnor_1_out, xor_1_out);
  xor xor_2 (xor_2_out, S6, C);
  // Probe on Result
  // Probe on Result
  Shifter #(.width(32)) shifter_1 (.in(X), .\dist (Y[4:0]), .out(shifter_1_out));
  Shifter #(.width(32), .shift("ar")) shifter_2 (.in(X), .\dist (Y[4:0]), .out(shifter_2_out));
  Shifter #(.width(32), .shift("lr")) shifter_3 (.in(X), .\dist (Y[4:0]), .out(shifter_3_out));
  Multiplier #(.width(32)) multiplier_1 (.a(X), .b(Y), .out(multiplier_1_out), .cout(multiplier_1_cout));  // open: cin
  Divider #(.width(32)) divider_1 (.a(X), .b(Y), .out(divider_1_out), .rem(divider_1_rem));  // open: upper
  _32bitadder u_32bitadder_1 (.in_1(X), .in_2({YY, multiplexer_1_out}), .C0(S6), .F({FF, n32bitadder_1_f}), .out_5(C));
  assign and_2_out = X & Y;  // AND_Gate and_2, 32 bits wide
  assign or_1_out = X | Y;  // OR_Gate or_1, 32 bits wide
  assign xor_3_out = X ^ Y;  // XOR_Gate xor_3, 32 bits wide
  assign nor_1_out = ~(X | Y);  // NOR_Gate nor_1, 32 bits wide
  Comparator #(.width(32)) comparator_3 (.a(X), .b(Y), .eq(Equal), .lt(comparator_3_lt[0]));  // open: gt
  Comparator #(.width(32), .mode("unsigned")) comparator_4 (.a(X), .b(Y), .lt(comparator_4_lt[0]));  // open: gt, eq
  or or_2 (or_2_out, S5, S6);
  Multiplexer #(.enable("false")) multiplexer_2 (.in0(1'b0), .in1(and_1_out), .out(Signed_Overflow), .sel(or_2_out));
  or or_3 (or_3_out, S5, S6);
  Multiplexer #(.enable("false")) multiplexer_3 (.in0(1'b0), .in1(xor_2_out), .out(UnSigned_Overflow), .sel(or_3_out));
  // Probe on Result_2
  Multiplexer #(.select(4), .width(32), .enable("false")) multiplexer_4 (
    .in0(shifter_1_out), .in1(shifter_2_out), .in2(shifter_3_out), .in3(multiplier_1_out),
    .in4(divider_1_out), .in5({FF, n32bitadder_1_f}), .in6({FF, n32bitadder_1_f}), .in7(and_2_out),
    .in8(or_1_out), .in9(xor_3_out), .in10(nor_1_out), .in11({{31{1'b0}}, comparator_3_lt[0]}),
    .in12({{31{1'b0}}, comparator_4_lt[0]}), .in13({32{1'b0}}), .in14({32{1'b0}}), .in15({32{1'b0}}),
    .out(Result), .sel(AluOP));
  Multiplexer #(.select(4), .width(32), .enable("false")) multiplexer_5 (
    .in0({32{1'b0}}), .in1({32{1'b0}}), .in2({32{1'b0}}), .in3(multiplier_1_cout), .in4(divider_1_rem),
    .in5({32{1'b0}}), .in6({32{1'b0}}), .in7({32{1'b0}}), .in8({32{1'b0}}), .in9({32{1'b0}}),
    .in10({32{1'b0}}), .in11({32{1'b0}}), .in12({32{1'b0}}), .in13({32{1'b0}}), .in14({32{1'b0}}),
    .in15({32{1'b0}}), .out(Result_2), .sel(AluOP));
  Comparator #(.width(32)) comparator_5 (.a(X), .b(Y), .gt(out), .eq(out_2), .lt(out_3));
  // Probe on n32bitadder_2_f
  _32bitadder u_32bitadder_2 (
    .in_1(X), .in_2(multiplexer_6_out), .C0(in_4), .F(n32bitadder_2_f), .out_5(n32bitadder_2_out_5));
  Multiplexer #(.width(32), .enable("false")) multiplexer_6 (
    .in0(Y), .in1(not_2_out), .out(multiplexer_6_out), .sel(in_4));
  // Probe on n32bitadder_2_out_5
  assign not_2_out = ~Y;  // NOT_Gate not_2, 32 bits wide

  // Other names for the same wires on the sheet: OF = Signed_Overflow; Result2[31:0] = Result_2; S[3:0] = AluOP;
  //   UOF = UnSigned_Overflow; XX = X[31]

  // Notes on the sheet:
  //   不要改变此引脚区域内容，也不要改变ALU封装形式
  //   输入引脚
  //   请在下方利用上方输入输出引脚的隧道信号构建ALU电路，ctrl+d复制选择部件
  //   华中科技大学计算机学院 计算机组成原理，鸣谢加州大学伯克利CS61C课程
  //   输出引脚
  //   探测区域
endmodule

module \我的等差数列  (
);

  wire clock_1_out;
  wire [31:0] alu_1_result, alu_2_result, register_1_q, S2;

  Clock clock_1 (.out(clock_1_out));
  // Probe on register_1_q
  Register #(.width(32)) register_1 (.D(alu_1_result), .Q(register_1_q), .clk(clock_1_out));  // open: en, clr
  // Probe on S2
  ALU alu_1 (
    .AluOP(4'b0101), .X(S2), .Result(alu_1_result), .Y(register_1_q));  // open: Equal, Signed_Overflow, Result_2, UnSigned_Overflow
  Register #(.width(32)) register_2 (.D(alu_2_result), .Q(S2), .clk(clock_1_out));  // open: en, clr
  ALU alu_2 (
    .AluOP(4'b0101), .X(S2), .Result(alu_2_result), .Y(32'h2));  // open: Equal, Signed_Overflow, Result_2, UnSigned_Overflow
  // Probe on alu_2_result
endmodule
