// Logisim project cpu.circ as structural Verilog: 13 circuits, main circuit main
// nop
module main (
);

  wire \_1号中断_out , \_2号中断_out , \_3号中断_out , ALUsrc, ALUsrc2, and_1_out, and_2_out, and_3_out, and_5_out,
       and_6_out, and_7_out, and_8_out, and_9_out, and_10_out, and_11_out, and_12_out, beq, beq2, beq3, bgtz,
       bgtz2, bgtz3, bne, bne2, bne3, branch, clk, clock_1_out, comparator_1_eq, comparator_3_lt, \end ,
       equal, eret, from1r1, from1r2, from1y, from2r1, from2r2, from2y, halt, IE, INS0, INS1, INS2, J, J2,
       J3, jal, jal2, jal3, jal4, Jr, Jr2, Jr3, load_nop, lui, lui2, lui3, lui4, main_1_p5, main_2_p7,
       main_2_p9, MemRead, MemRead2, MemRead3, MemtoReg, MemtoReg2, MemtoReg3, MemtoReg4, MemWrite,
       MemWrite2, MemWrite3, mfc0, mtc0, nop, nor_1_out, nor_2_out, not_1_out, not_2_out, not_5_out,
       not_6_out, not_7_out, not_8_out, or_1_out, or_4_out, or_7_out, pcc, RegDst, RegDst2, register_4_q,
       Regwrite, Regwrite2, Regwrite3, Regwrite4, \R型指令 , sb, sb2, sb3, sel0, sel1, sel2, sel3, shift,
       shift2, sys4, \中断_1_led1 , \中断_1_led2 , \中断_1_led3 ;
  wire [1:0] iterNo;
  wire [3:0] ALUop, ALUop2;
  wire [4:0] multiplexer_3_out, multiplexer_4_out, multiplexer_7_out, multiplexer_8_out, multiplexer_9_out,
       multiplexer_10_out, multiplexer_15_out, multiplexer_17_out, multiplexer_24_out, multiplexer_27_out,
       rd0, rd2, rs0, rs2, rt2, writereg2, writereg3, writereg4;
  wire [5:0] redirection_1_from1r1;
  wire [7:0] multiplexer_33_out, multiplexer_34_out, multiplexer_36_out;
  wire [15:0] im;
  wire [18:0] singal;
  wire [27:0] ins_shift2, shifter_1_out;
  wire [31:0] a0, adder_2_out, adder_3_out, addr_01, bit_extender_1_out, bit_extender_2_out,
       bit_extender_3_out, C1, counter_1_q, counter_2_q, EPC, extend_im2, im0, im2, im3, ins2_t, ins3, ins_0,
       main_1_p8, mem_data_out, memdate, memdate0, multiplexer_1_out, multiplexer_5_out, multiplexer_6_out,
       multiplexer_14_out, multiplexer_19_out, multiplexer_21_out, multiplexer_22_out, multiplexer_25_out,
       multiplexer_26_out, multiplexer_32_out, multiplexer_35_out, multiplexer_37_out, multiplexer_38_out,
       multiplexer_40_out, multiplexer_41_out, multiplexer_42_out, PC, PC0, PC2, PC3, PC4, pc_0, pc_40,
       pc_in, R1, R2, R12, R13, R22, reddate, result0, s0, s1, s2, shifter_2_out, shifter_3_out, singal2,
       singal3, writeback, writeback0, X, XX, Y, YY;
  wire [31:16] ins;

  Hex_Digit_Display hex_digit_display_1 (.value(a0[31:28]));  // open: dp
  // Probe on multiplexer_32_out
  // Probe on multiplexer_1_out
  nor nor_1 (nor_1_out, INS0, INS1, \end );
  Comparator #(.width(32)) comparator_1 (.a(32'ha), .b(s0), .eq(comparator_1_eq));  // open: gt, lt
  // Probe on s0
  // Probe on pc_40
  // Probe on R1
  // Probe on s0
  Hex_Digit_Display hex_digit_display_2 (.value(a0[27:24]));  // open: dp
  Hex_Digit_Display hex_digit_display_3 (.value(a0[23:20]));  // open: dp
  Multiplexer #(.width(32), .enable("false")) multiplexer_1 (
    .in0(multiplexer_32_out), .in1(EPC), .out(multiplexer_1_out), .sel(eret));
  Multiplexer #(.width(32), .enable("false")) multiplexer_2 (
    .in0(pc_40), .in1(multiplexer_1_out), .out(pc_in), .sel(pcc));
  and and_1 (and_1_out, nor_1_out, ~load_nop);  // AND_Gate
  and and_2 (and_2_out, clk, not_1_out);
  not not_1 (not_1_out, halt);
  Clock clock_1 (.out(clock_1_out));
  and and_3 (and_3_out, comparator_1_eq, sys4);
  // Probe on PC
  // Probe on R2
  // Probe on s1
  Hex_Digit_Display hex_digit_display_4 (.value(a0[15:12]));  // open: dp
  Hex_Digit_Display hex_digit_display_5 (.value(a0[19:16]));  // open: dp
  cp0 cp0_1 (
    .op5(ins[31]), .op4(ins[30]), .op3(ins[29]), .op2(ins[28]), .op1(ins[27]), .op0(ins[26]), .m4(ins[25]),
    .m3(ins[24]), .m2(ins[23]), .m1(ins[22]), .m0(ins[21]), .eret(eret), .mfc0(mfc0), .mtc0(mtc0));
  // Probe on EPC
  Register #(.width(32)) u_PC (.D(pc_in), .en(and_1_out), .Q(pc_0), .clk(and_2_out), .clr(INS2));
  and and_4 (clk, not_1_out, clock_1_out);
  Register #(.width(1)) register_1 (.D(1'b1), .en(and_3_out), .Q(halt), .clk(clk));  // open: clr
  // Probe on PC2
  // Probe on s1
  // Probe on s2
  Hex_Digit_Display hex_digit_display_6 (.value(a0[7:4]));  // open: dp
  Hex_Digit_Display hex_digit_display_7 (.value(a0[11:8]));  // open: dp
  Adder #(.width(32)) adder_1 (.a(32'h4), .b(pc_0), .out(pc_40));  // open: cin, cout
  // Probe on pc_0[11:2]
  nor nor_2 (nor_2_out, INS0, INS1, INS2, \end );
  // Probe on PC3
  // Probe on s2
  // Probe on R1
  Hex_Digit_Display hex_digit_display_8 (.value(a0[3:0]));  // open: dp
  instruction instruction_1 (.instructionin(pc_0[11:2]), .instructionout(ins_0), .iterNo(iterNo), .enable(nor_2_out));
  // Probe on load_nop
  // Probe on im[15:11]
  // Probe on pc_40
  // Probe on iterNo
  Counter #(.width(32), .max('hffffffff)) counter_1 (.Q(counter_1_q), .clk(clk));  // open: load, D, count, carry, clr
  // Probe on addr_01[25:2]
  // Probe on R2
  Multiplexer #(.width(5), .enable("false")) multiplexer_3 (
    .in0(im[15:11]), .in1(5'b10010), .out(multiplexer_3_out), .sel(INS1));
  // Probe on ins_0
  // Probe on counter_1_q
  // Probe on memdate
  // Probe on X
  and and_5 (and_5_out, clk, not_2_out);
  not not_2 (not_2_out, halt);
  // Probe on EPC
  Multiplexer #(.width(5), .enable("false")) multiplexer_4 (
    .in0(multiplexer_3_out), .in1({5{1'b1}}), .out(multiplexer_4_out), .sel(INS0));
  // Probe on multiplexer_4_out
  // Probe on R2
  or or_1 (or_1_out, load_nop, pcc);
  IF_ID IF_ID (.pc_next(pc_40), .pc(ins_0), .out_6(PC), .out_7({ins, im}), .clk(clk), .nop(load_nop), .clear(or_1_out));
  // Probe on MemWrite3
  // Probe on Y
  // Probe on counter_2_q
  Counter #(.width(32), .max('hffffffff)) counter_2 (
    .count(load_nop), .Q(counter_2_q), .clk(and_5_out));  // open: load, D, carry, clr
  // Probe on multiplexer_5_out
  Multiplexer #(.width(32), .enable("false")) multiplexer_5 (
    .in0(multiplexer_6_out), .in1(32'h1), .out(multiplexer_5_out), .sel(INS0));
  Multiplexer #(.width(32), .enable("false")) multiplexer_6 (.in0(R2), .in1(PC0), .out(multiplexer_6_out), .sel(INS1));
  // Probe on PC
  // Probe on {ins, im}
  // ACM1401_U201414623_周杨杰_regfile_main main_1: pin names not known; wires that end beside it: EPC, im[15:11], multiplexer_4_out, multiplexer_5_out, main_1_p5, EPC, clk, main_1_p8, C1, main_1_p8[0]
  or or_2 (main_1_p5, INS0, mtc0, INS1);
  // Probe on addr_01
  not not_3 (IE, main_1_p8[0]);
  Shifter #(.width(28)) shifter_1 (.in({ins[27:16], im}), .\dist (5'b00010), .out(shifter_1_out));
  \运算器控制  \u_运算器控制_1  (
    .op5(ins[31]), .op4(ins[30]), .op3(ins[29]), .op2(ins[28]), .op1(ins[27]), .op0(ins[26]), .f5(im[5]),
    .f4(im[4]), .f3(im[3]), .f2(im[2]), .f1(im[1]), .f0(im[0]), .AluSrc(ALUsrc), .AluCtrl3(ALUop[3]),
    .AluCtrl2(ALUop[2]), .AluCtrl1(ALUop[1]), .AluCtrl0(ALUop[0]), .sys(singal[17]), .srav(singal[18]),
    .lui(lui), .sb(sb), .bgtz(bgtz));
  \控制器  \u_控制器_1  (
    .op5(ins[31]), .op4(ins[30]), .op3(ins[29]), .op2(ins[28]), .op1(ins[27]), .op0(ins[26]), .f5(im[5]),
    .f4(im[4]), .f3(im[3]), .f2(im[2]), .f1(im[1]), .f0(im[0]), .Zeroextend(singal[0]), .RegDst(RegDst),
    .Shift(shift), .j(J), .jal(jal), .jr(Jr), .beq(beq), .bne(bne), .MemRead(MemRead), .MemtoReg(MemtoReg),
    .MemWrite(MemWrite), .RegWrite(Regwrite));
  Multiplexer #(.width(5), .enable("false")) multiplexer_7 (
    .in0(ins[25:21]), .in1(ins[20:16]), .out(multiplexer_7_out), .sel(shift));
  Multiplexer #(.width(5), .enable("false")) multiplexer_8 (
    .in0(multiplexer_7_out), .in1({5{1'b1}}), .out(multiplexer_8_out), .sel(Jr));
  Multiplexer #(.width(5), .enable("false")) multiplexer_9 (
    .in0(ins[20:16]), .in1(im[15:11]), .out(multiplexer_9_out), .sel(RegDst));
  Multiplexer #(.width(5), .enable("false")) multiplexer_10 (
    .in0(multiplexer_9_out), .in1({5{1'b1}}), .out(multiplexer_10_out), .sel(jal));
  assign bit_extender_1_out = {{16{im[15]}}, im};  // Bit_Extender bit_extender_1
  Multiplexer #(.width(32), .enable("false")) multiplexer_11 (
    .in0(bit_extender_1_out), .in1(bit_extender_2_out), .out(im0), .sel(singal[0]));
  assign bit_extender_2_out = {{16{1'b0}}, im};  // Bit_Extender bit_extender_2
  assign bit_extender_3_out = {{27{1'b0}}, im[10:6]};  // Bit_Extender bit_extender_3
  // Probe on writereg3
  Multiplexer #(.width(5), .enable("false")) multiplexer_12 (
    .in0(multiplexer_8_out), .in1(5'b00010), .out(rs0), .sel(singal[17]));
  Multiplexer #(.width(5), .enable("false")) multiplexer_13 (
    .in0(multiplexer_10_out), .in1(ins[20:16]), .out(rd0), .sel(mfc0));
  // Probe on im0
  // Probe on writereg2
  // Probe on ins[20:16]
  // Probe on rs0
  // ACM1401_U201414623_周杨杰_regfile_main main_2: pin names not known; wires that end beside it: rs0, ins[20:16], writereg4, s0, writeback, s1, main_2_p7, s2, main_2_p9, a0, R1, R2
  or or_3 (main_2_p7, mfc0, Regwrite4);
  not not_4 (main_2_p9, clk);
  redirection redirection_1 (
    .from1R1(redirection_1_from1r1[0]), .nop(load_nop), .from1Y(redirection_1_from1r1[1]), .rt(ins[20:16]),
    .from1R2(redirection_1_from1r1[2]), .shift(shift), .Regwrite(Regwrite2), .MemtoReg(MemtoReg2),
    .from2R1(redirection_1_from1r1[3]), .writereg1(writereg3), .from2Y(redirection_1_from1r1[4]),
    .from2R2(redirection_1_from1r1[5]), .Regwrite3(Regwrite3), .writereg0(writereg2), .rs(rs0),
    .ALUsrc(ALUsrc));
  Button \_1号中断  (.out(\_1号中断_out ));
  LED \_1号中断等待指示灯  (.in(\中断_1_led1 ));
  Button \_2号中断  (.out(\_2号中断_out ));
  LED \_1号中断等待指示灯_2  (.in(\中断_1_led2 ));
  Button \_3号中断  (.out(\_3号中断_out ));
  LED \_1号中断等待指示灯_3  (.in(\中断_1_led3 ));
  // Probe on R1
  // Probe on rd0
  \中断  \u_中断_1  (
    .IR1(\_1号中断_out ), .IR2(\_2号中断_out ), .IR3(\_3号中断_out ), .IntNo(iterNo), .clk(clk), .ret(\end ), .ie(IE),
    .INT1(INS0), .INT2(INS1), .INT3(INS2), .LED1(\中断_1_led1 ), .LED2(\中断_1_led2 ), .LED3(\中断_1_led3 ),
    .in_7(IE));
  or or_4 (or_4_out, load_nop, pcc);
  // ID_EX ID_EX: pin names not known; wires that end beside it: shifter_1_out, PC, {ins, im}, {{7{1'b0}}, eret, mtc0, mfc0, bgtz, sb, lui, singal[18:17], ALUop, ALUsrc, Regwrite, MemWrite, MemtoReg, MemRead, bne, beq, Jr, jal, J, shift, RegDst, singal[0]}, R1, R2, rd0, im0, bit_extender_3_out, load_nop, clk, or_4_out, ins_shift2, PC2, ins2_t, {singal2[31:22], bgtz2, sb2, lui2, singal2[18:17], ALUop2, ALUsrc2, Regwrite2, MemWrite2, MemtoReg2, MemRead2, bne2, beq2, Jr2, jal2, J2, shift2, RegDst2, singal2[0]}, R12, R22, writereg2, im2, extend_im2
  // Probe on R2
  Register #(.width(6)) register_2 (
    .D(redirection_1_from1r1), .Q({from2r2, from2y, from2r1, from1r2, from1y, from1r1}), .clk(clk));  // open: en, clr
  Register #(.width(1)) register_3 (.D(eret), .Q(\end ), .clk(clk), .clr(register_4_q));  // open: en
  // Probe on iterNo
  Register #(.width(1)) register_4 (.D(\end ), .Q(register_4_q), .clk(clk));  // open: en, clr
  // Probe on R12
  Multiplexer #(.width(32), .enable("false")) multiplexer_14 (
    .in0(R22), .in1(im2), .out(multiplexer_14_out), .sel(ALUsrc2));
  Multiplexer #(.width(5), .enable("false")) multiplexer_15 (
    .in0(ins2_t[20:16]), .in1(ins2_t[15:11]), .out(multiplexer_15_out), .sel(RegDst2));
  Multiplexer #(.width(5), .enable("false")) multiplexer_16 (
    .in0(multiplexer_15_out), .in1({5{1'b1}}), .out(rd2), .sel(jal2));
  Multiplexer #(.width(5), .enable("false")) multiplexer_17 (
    .in0(ins2_t[25:21]), .in1(ins2_t[20:16]), .out(multiplexer_17_out), .sel(singal2[18]));
  Multiplexer #(.width(5), .enable("false")) multiplexer_18 (
    .in0(ins2_t[20:16]), .in1(ins2_t[25:21]), .out(rt2), .sel(singal2[18]));
  Multiplexer #(.width(32), .enable("false")) multiplexer_19 (
    .in0(R12), .in1(reddate), .out(multiplexer_19_out), .sel(from1r1));
  Multiplexer #(.width(32), .enable("false")) multiplexer_20 (
    .in0(multiplexer_19_out), .in1(writeback), .out(XX), .sel(from2r1));
  Multiplexer #(.width(32), .enable("false")) multiplexer_21 (
    .in0(multiplexer_22_out), .in1(32'ha), .out(multiplexer_21_out), .sel(singal2[17]));
  Multiplexer #(.width(32), .enable("false")) multiplexer_22 (
    .in0(multiplexer_14_out), .in1(extend_im2), .out(multiplexer_22_out), .sel(shift2));
  Multiplexer #(.width(32), .enable("false")) multiplexer_23 (.in0(XX), .in1(YY), .out(X), .sel(singal2[18]));
  Multiplexer #(.width(5), .enable("false")) multiplexer_24 (
    .in0(multiplexer_17_out), .in1(ins2_t[20:16]), .out(multiplexer_24_out), .sel(shift2));
  // Probe on R12
  // Probe on XX
  Multiplexer #(.width(32), .enable("false")) multiplexer_25 (
    .in0(multiplexer_21_out), .in1(writeback), .out(multiplexer_25_out), .sel(from2y));
  Multiplexer #(.width(32), .enable("false")) multiplexer_26 (
    .in0(R22), .in1(writeback), .out(multiplexer_26_out), .sel(from2r2));
  Multiplexer #(.width(5), .enable("false")) multiplexer_27 (
    .in0(multiplexer_24_out), .in1({5{1'b1}}), .out(multiplexer_27_out), .sel(Jr2));
  Multiplexer #(.width(32), .enable("false")) multiplexer_28 (
    .in0(multiplexer_25_out), .in1(reddate), .out(YY), .sel(from1y));
  Multiplexer #(.width(32), .enable("false")) multiplexer_29 (.in0(YY), .in1(XX), .out(Y), .sel(singal2[18]));
  Multiplexer #(.width(32), .enable("false")) multiplexer_30 (
    .in0(multiplexer_26_out), .in1(reddate), .out(memdate0), .sel(from1r2));
  Multiplexer #(.width(5), .enable("false")) multiplexer_31 (
    .in0(multiplexer_27_out), .in1(5'b00010), .out(rs2), .sel(singal2[17]));
  ALU alu_1 (
    .AluOP(ALUop2), .X(X), .Equal(equal), .Result(result0), .Y(Y));  // open: Signed_Overflow, Result_2, UnSigned_Overflow
  // Probe on memdate0
  or or_5 (pcc, eret, Jr2, jal2, J2, bgtz2, branch);
  EX_MEM EX_MEM (
    .signal(ins2_t), .R1(PC2), .writeback(result0), .in_10(im2), .in_11(memdate0), .out_17(ins3),
    .out_19(PC3), .out_21(addr_01), .out_22(im3), .out_23(memdate), .clk(clk),
    .in_4({singal2[31:22], bgtz2, sb2, lui2, singal2[18:17], ALUop2, ALUsrc2, Regwrite2, MemWrite2, MemtoReg2, MemRead2, bne2, beq2, Jr2, jal2, J2, shift2, RegDst2, singal2[0]}),
    .out_16({singal3[31:22], bgtz3, sb3, lui3, singal3[18:12], Regwrite3, MemWrite3, MemtoReg3, MemRead3, bne3, beq3, Jr3, jal3, J3, singal3[2:0]}),
    .in_14(R12), .out_26(R13), .in_15(writereg2), .out_27(writereg3));  // open: pc, R2, out_18, out_20, in_12, out_24, in_13, out_25, nop, clear
  // Probe on writereg2
  Comparator #(.width(6)) comparator_2 (.a(ins[31:26]), .b({6{1'b0}}), .eq(\R型指令 ));  // open: gt, lt
  // Probe on ins[20:16]
  // Probe on addr_01
  // Probe on memdate
  // Probe on \R型指令 
  // Probe on rs0
  pop pop_1 (
    .RW_EX(writereg2), .RegWrite_EX(Regwrite2), .RW_MEM(writereg3), .RegWrite_MEM(Regwrite3),
    .RW_WB(writereg4), .RegWrite_WB(Regwrite4), .beq(beq), .bne(bne), .\R型指令 (\R型指令 ), .jr(Jr), .lui(lui),
    .ALUsrc(ALUsrc), .shift(shift), .bgtz(bgtz), .SysCall(singal[17]), .RT(ins[20:16]), .RS(rs0), .nop(nop));
  Shifter #(.width(32)) shifter_2 (.in(im2), .\dist (5'b00010), .out(shifter_2_out));
  and and_6 (and_6_out, bgtz2, comparator_3_lt);
  Multiplexer #(.width(32), .enable("false")) multiplexer_32 (
    .in0(multiplexer_38_out), .in1(adder_3_out), .out(multiplexer_32_out), .sel(and_6_out));
  // Probe on shifter_2_out
  Multiplexer #(.width(8), .enable("false")) multiplexer_33 (
    .in0(memdate[15:8]), .in1(memdate[7:0]), .out(multiplexer_33_out), .sel(sb3));
  Multiplexer #(.width(8), .enable("false")) multiplexer_34 (
    .in0(memdate[31:24]), .in1(memdate[7:0]), .out(multiplexer_34_out), .sel(sb3));
  // Probe on PC2
  Comparator #(.width(32)) comparator_3 (.a({32{1'b0}}), .b(X), .lt(comparator_3_lt));  // open: gt, eq
  Adder #(.width(32)) adder_2 (.a(PC2), .b(shifter_2_out), .out(adder_2_out));  // open: cin, cout
  and and_7 (and_7_out, bne2, not_5_out);
  not not_5 (not_5_out, equal);
  and and_8 (and_8_out, beq2, equal);
  Adder #(.width(32)) adder_3 (.a(PC2), .b(shifter_2_out), .out(adder_3_out));  // open: cin, cout
  Multiplexer #(.width(32), .enable("false")) multiplexer_35 (
    .in0(PC2), .in1(adder_2_out), .out(multiplexer_35_out), .sel(branch));
  or or_6 (branch, and_7_out, and_8_out);
  RAM #(.addrWidth(24), .bus("separate")) ram_1 (
    .addr(addr_01[25:2]), .din(multiplexer_33_out), .data(mem_data_out[15:8]), .str(MemWrite3), .sel(sel1),
    .clk(clk), .ld(MemRead3));  // open: clr
  RAM #(.addrWidth(24), .bus("separate")) ram_2 (
    .addr(addr_01[25:2]), .din(multiplexer_34_out), .data(mem_data_out[31:24]), .str(MemWrite3), .sel(sel3),
    .clk(clk), .ld(MemRead3));  // open: clr
  Multiplexer #(.width(8), .enable("false")) multiplexer_36 (
    .in0(memdate[23:16]), .in1(memdate[7:0]), .out(multiplexer_36_out), .sel(sb3));
  or or_7 (or_7_out, jal2, J2);
  // Probe on mem_data_out[15:8]
  // Probe on mem_data_out[31:24]
  Multiplexer #(.width(32), .enable("false")) multiplexer_37 (
    .in0(multiplexer_35_out), .in1({PC2[31:28], ins_shift2}), .out(multiplexer_37_out), .sel(or_7_out));
  // Probe on {PC2[31:28], ins_shift2}
  // Probe on mem_data_out[7:0]
  RAM #(.addrWidth(24), .bus("separate")) ram_3 (
    .addr(addr_01[25:2]), .din(memdate[7:0]), .data(mem_data_out[7:0]), .str(MemWrite3), .sel(sel0),
    .clk(clk), .ld(MemRead3));  // open: clr
  // Probe on multiplexer_38_out
  Multiplexer #(.width(32), .enable("false")) multiplexer_38 (
    .in0(multiplexer_37_out), .in1(R12), .out(multiplexer_38_out), .sel(Jr2));
  // Probe on mem_data_out[23:16]
  RAM #(.addrWidth(24), .bus("separate")) ram_4 (
    .addr(addr_01[25:2]), .din(multiplexer_36_out), .data(mem_data_out[23:16]), .str(MemWrite3), .sel(sel2),
    .clk(clk), .ld(MemRead3));  // open: clr
  // Probe on addr_01
  Multiplexer #(.width(32), .enable("false")) multiplexer_39 (
    .in0(addr_01), .in1(mem_data_out), .out(reddate), .sel(MemRead3));
  Multiplexer #(.width(32), .enable("false")) multiplexer_40 (
    .in0(addr_01), .in1(mem_data_out), .out(multiplexer_40_out), .sel(MemtoReg3));
  Shifter #(.width(32)) shifter_3 (.in(im3), .\dist (5'b10000), .out(shifter_3_out));
  Multiplexer #(.width(32), .enable("false")) multiplexer_41 (
    .in0(multiplexer_40_out), .in1(shifter_3_out), .out(multiplexer_41_out), .sel(lui3));
  Multiplexer #(.width(32), .enable("false")) multiplexer_42 (
    .in0(multiplexer_41_out), .in1(C1), .out(multiplexer_42_out), .sel(mfc0));
  Multiplexer #(.width(32), .enable("false")) multiplexer_43 (
    .in0(multiplexer_42_out), .in1(PC3), .out(writeback0), .sel(jal3));
  not not_6 (not_6_out, addr_01[0]);
  not not_7 (not_7_out, addr_01[1]);
  not not_8 (not_8_out, sb3);
  and and_9 (and_9_out, not_6_out, not_7_out);
  and and_10 (and_10_out, not_6_out, addr_01[1]);
  and and_11 (and_11_out, addr_01[0], not_7_out);
  and and_12 (and_12_out, addr_01[1], addr_01[0]);
  MEM_WB MEM_WB (
    .in_4(PC3), .out_14(PC4), .clk(clk), .in_6(writeback0), .out_16(writeback), .in_7(jal3), .out_17(jal4),
    .in_8(lui3), .out_18(lui4), .in_9(writereg3), .out_19(writereg4), .in_11(MemtoReg3), .out_21(MemtoReg4),
    .in_12(singal3[17]), .out_22(sys4), .in_13(Regwrite3), .out_23(Regwrite4));  // open: in_5, out_15, in_10, out_20, nop, clear
  or or_8 (sel0, not_8_out, and_9_out);
  or or_9 (sel1, and_10_out, not_8_out);
  or or_10 (sel2, and_11_out, not_8_out);
  or or_11 (sel3, and_12_out, not_8_out);

  // Other names for the same wires on the sheet: ins[15:0] = im; rd[4:0] = im[15:11]; rt[4:0] = ins[20:16];
  //   rs[4:0] = ins[25:21]; op[5:0] = ins[31:26]; result[31:0] = addr_01; memaddr[23:0] = addr_01[25:2];
  //   Zero_extend = singal[0];
  //   singal (some bits) = {eret, mtc0, mfc0, bgtz, sb, lui, ALUop, ALUsrc, Regwrite, MemWrite, MemtoReg, MemRead, bne, beq, Jr, jal, J, shift, RegDst};
  //   sys = singal[17]; srav = singal[18];
  //   singal2 (some bits) = {bgtz2, sb2, lui2, ALUop2, ALUsrc2, Regwrite2, MemWrite2, MemtoReg2, MemRead2, bne2, beq2, Jr2, jal2, J2, shift2, RegDst2};
  //   sys2 = singal2[17]; srav2 = singal2[18];
  //   singal3 (some bits) = {bgtz3, sb3, lui3, Regwrite3, MemWrite3, MemtoReg3, MemRead3, bne3, beq3, Jr3, jal3, J3};
  //   sys3 = singal3[17]; srav3 = singal3[18]; writereg1[4:0] = rd0
endmodule

module \运算器控制  (
  input  op5,
  input  op4,
  input  op3,
  input  op2,
  input  op1,
  input  op0,
  input  f5,
  input  f4,
  input  f3,
  input  f2,
  input  f1,
  input  f0,
  output AluSrc,
  output AluCtrl3,
  output AluCtrl2,
  output AluCtrl1,
  output AluCtrl0,
  output sys,
  output srav,
  output lui,
  output sb,
  output bgtz
);

  wire and_1_out, and_2_out, and_3_out, and_4_out, and_5_out, and_6_out, and_7_out, and_8_out, and_9_out,
       and_10_out, and_11_out, and_12_out, and_13_out, and_14_out, and_15_out, and_16_out, and_17_out,
       and_18_out, and_19_out, and_20_out, and_21_out, and_22_out, and_23_out, and_24_out, and_25_out,
       and_26_out, and_27_out, and_28_out, and_29_out, and_30_out, and_31_out, and_32_out, and_33_out,
       and_34_out, and_35_out, and_36_out, and_37_out, and_38_out, and_39_out, and_40_out, and_41_out,
       and_42_out, and_43_out, and_44_out, and_45_out, and_46_out, and_47_out, and_48_out, and_49_out,
       and_50_out, and_51_out, not_1_out, not_2_out, not_3_out, not_4_out, not_5_out, not_6_out, not_7_out,
       not_8_out, not_9_out, not_10_out, not_11_out, not_12_out, not_13_out, not_14_out, not_15_out,
       not_16_out, not_17_out, not_18_out, not_19_out, not_20_out, not_21_out, not_22_out, not_23_out,
       not_24_out, not_25_out, not_26_out, not_27_out, not_28_out, not_29_out, not_30_out, not_31_out,
       not_32_out, not_33_out, not_34_out, not_35_out, not_36_out, not_37_out, not_38_out, not_39_out,
       not_40_out, not_41_out, not_42_out, not_43_out, not_44_out, not_45_out, not_46_out, not_47_out,
       not_48_out, not_49_out, not_50_out, not_51_out, not_52_out, not_53_out, not_54_out, not_55_out,
       not_56_out, not_57_out, not_58_out, not_59_out, not_60_out, not_61_out, not_62_out, not_63_out,
       not_64_out, not_65_out, not_66_out, not_67_out, not_68_out, not_69_out, not_70_out, not_71_out,
       not_72_out, not_73_out, not_74_out, not_75_out, not_76_out, not_77_out, not_78_out, not_79_out,
       not_80_out, not_81_out, not_82_out, not_83_out, not_84_out, not_85_out, not_86_out, not_87_out,
       not_88_out, not_89_out, not_90_out, not_91_out, not_92_out, not_93_out, not_94_out, not_95_out,
       not_96_out, not_97_out, not_98_out, not_99_out, not_100_out, not_101_out, not_102_out, not_103_out,
       not_104_out, not_105_out, not_106_out, not_107_out, not_108_out, not_109_out, not_110_out,
       not_111_out, not_112_out, not_113_out, not_114_out, not_115_out, not_116_out, not_117_out,
       not_118_out, not_119_out, not_120_out, not_121_out, not_122_out, not_123_out, not_124_out,
       not_125_out, not_126_out, not_127_out, not_128_out, not_129_out, not_130_out, not_131_out,
       not_132_out, not_133_out, not_134_out, not_135_out, not_136_out, not_137_out, not_138_out,
       not_139_out, not_140_out, not_141_out, not_142_out, not_143_out, not_144_out, not_145_out,
       not_146_out, not_147_out, not_148_out, not_149_out, not_150_out, not_151_out, not_152_out,
       not_153_out, not_154_out, not_155_out, not_156_out, not_157_out, not_158_out, not_159_out,
       not_160_out, not_161_out, not_162_out, not_163_out, not_164_out, not_165_out, not_166_out,
       not_167_out, not_168_out, not_169_out, not_170_out, not_171_out, not_172_out, not_173_out,
       not_174_out, not_175_out, not_176_out, not_177_out, not_178_out, not_179_out, not_180_out,
       not_181_out, not_182_out, not_183_out, not_184_out, not_185_out, not_186_out, not_187_out,
       not_188_out, not_189_out, not_190_out, not_191_out, not_192_out, not_193_out, not_194_out,
       not_195_out, not_196_out, not_197_out, not_198_out, not_199_out, not_200_out, not_201_out,
       not_202_out, not_203_out, not_204_out, not_205_out, not_206_out, not_207_out, not_208_out,
       not_209_out, not_210_out, not_211_out, not_212_out, not_213_out, not_214_out, not_215_out,
       not_216_out, not_217_out, not_218_out, not_219_out, not_220_out, not_221_out, not_222_out,
       not_223_out, not_224_out, not_225_out, not_226_out, not_227_out, not_228_out, not_229_out,
       not_230_out, not_231_out, not_232_out, not_233_out, not_234_out, not_235_out, not_236_out,
       not_237_out, not_238_out, not_239_out, not_240_out, not_241_out, not_242_out, not_243_out,
       not_244_out, not_245_out, not_246_out, not_247_out, not_248_out, not_249_out, not_250_out,
       not_251_out, not_252_out, not_253_out, not_254_out, not_255_out, not_256_out, not_257_out,
       not_258_out, not_259_out, not_260_out, not_261_out, not_262_out, not_263_out, not_264_out,
       not_265_out, not_266_out, not_267_out, not_268_out, not_269_out, not_270_out, not_271_out,
       not_272_out, not_273_out, not_274_out, not_275_out, not_276_out, not_277_out, not_278_out,
       not_279_out, not_280_out, not_281_out, not_282_out, not_283_out, not_284_out, not_285_out,
       not_286_out, not_287_out, not_288_out, not_289_out, not_290_out, not_291_out, not_292_out,
       not_293_out, not_294_out, not_295_out, not_296_out, not_297_out, not_298_out, not_299_out,
       not_300_out, not_301_out, not_302_out, not_303_out, not_304_out, not_305_out, not_306_out,
       not_307_out, not_308_out, not_309_out, not_310_out, not_311_out, not_312_out, not_313_out,
       not_314_out, not_315_out, not_316_out, not_317_out, not_318_out, not_319_out, not_320_out,
       not_321_out, not_322_out, not_323_out, not_324_out, not_325_out, not_326_out, not_327_out,
       not_328_out, not_329_out, not_330_out, not_331_out, not_332_out, not_333_out, not_334_out,
       not_335_out, not_336_out, not_337_out, not_338_out, not_339_out, not_340_out, not_341_out,
       not_342_out, not_343_out, not_344_out, not_345_out, not_346_out, not_347_out, not_348_out,
       not_349_out, not_350_out, not_351_out, not_352_out, not_353_out;

  not not_1 (not_1_out, op5);
  not not_2 (not_2_out, op4);
  not not_3 (not_3_out, op2);
  not not_4 (not_4_out, op1);
  not not_5 (not_5_out, op0);
  not not_6 (not_6_out, op5);
  not not_7 (not_7_out, op4);
  not not_8 (not_8_out, op2);
  not not_9 (not_9_out, op1);
  not not_10 (not_10_out, op5);
  not not_11 (not_11_out, op4);
  not not_12 (not_12_out, op1);
  not not_13 (not_13_out, op0);
  not not_14 (not_14_out, op5);
  not not_15 (not_15_out, op4);
  not not_16 (not_16_out, op1);
  not not_17 (not_17_out, op4);
  not not_18 (not_18_out, op3);
  not not_19 (not_19_out, op2);
  not not_20 (not_20_out, op4);
  not not_21 (not_21_out, op2);
  not not_22 (not_22_out, op5);
  not not_23 (not_23_out, op4);
  not not_24 (not_24_out, op2);
  not not_25 (not_25_out, op0);
  not not_26 (not_26_out, op5);
  not not_27 (not_27_out, op4);
  not not_28 (not_28_out, op3);
  not not_29 (not_29_out, op2);
  not not_30 (not_30_out, op1);
  not not_31 (not_31_out, op0);
  not not_32 (not_32_out, f5);
  not not_33 (not_33_out, f4);
  not not_34 (not_34_out, f3);
  not not_35 (not_35_out, f2);
  not not_36 (not_36_out, f1);
  not not_37 (not_37_out, f0);
  not not_38 (not_38_out, op5);
  not not_39 (not_39_out, op4);
  not not_40 (not_40_out, op3);
  not not_41 (not_41_out, op2);
  not not_42 (not_42_out, op1);
  not not_43 (not_43_out, op0);
  not not_44 (not_44_out, f5);
  not not_45 (not_45_out, f4);
  not not_46 (not_46_out, f3);
  not not_47 (not_47_out, f2);
  not not_48 (not_48_out, op5);
  not not_49 (not_49_out, op4);
  not not_50 (not_50_out, op3);
  not not_51 (not_51_out, op2);
  not not_52 (not_52_out, op1);
  not not_53 (not_53_out, op0);
  not not_54 (not_54_out, f5);
  not not_55 (not_55_out, f4);
  not not_56 (not_56_out, f3);
  not not_57 (not_57_out, f2);
  not not_58 (not_58_out, f0);
  not not_59 (not_59_out, op5);
  not not_60 (not_60_out, op4);
  not not_61 (not_61_out, op4);
  not not_62 (not_62_out, op2);
  not not_63 (not_63_out, op1);
  not not_64 (not_64_out, op0);
  not not_65 (not_65_out, op5);
  not not_66 (not_66_out, op4);
  not not_67 (not_67_out, op1);
  not not_68 (not_68_out, op5);
  not not_69 (not_69_out, op4);
  not not_70 (not_70_out, op2);
  not not_71 (not_71_out, op0);
  not not_72 (not_72_out, op5);
  not not_73 (not_73_out, op4);
  not not_74 (not_74_out, op3);
  not not_75 (not_75_out, op2);
  not not_76 (not_76_out, op1);
  not not_77 (not_77_out, op0);
  not not_78 (not_78_out, f4);
  not not_79 (not_79_out, f3);
  not not_80 (not_80_out, f1);
  not not_81 (not_81_out, op5);
  not not_82 (not_82_out, op4);
  not not_83 (not_83_out, op3);
  not not_84 (not_84_out, op2);
  not not_85 (not_85_out, op1);
  not not_86 (not_86_out, op0);
  not not_87 (not_87_out, f4);
  not not_88 (not_88_out, f3);
  not not_89 (not_89_out, op5);
  not not_90 (not_90_out, op4);
  not not_91 (not_91_out, op3);
  not not_92 (not_92_out, op2);
  not not_93 (not_93_out, op1);
  not not_94 (not_94_out, op0);
  not not_95 (not_95_out, f4);
  not not_96 (not_96_out, f2);
  not not_97 (not_97_out, f0);
  not not_98 (not_98_out, op5);
  not not_99 (not_99_out, op4);
  not not_100 (not_100_out, op3);
  not not_101 (not_101_out, op2);
  not not_102 (not_102_out, op1);
  not not_103 (not_103_out, op0);
  not not_104 (not_104_out, f4);
  not not_105 (not_105_out, f2);
  not not_106 (not_106_out, op5);
  not not_107 (not_107_out, op4);
  not not_108 (not_108_out, op2);
  not not_109 (not_109_out, op1);
  not not_110 (not_110_out, op0);
  not not_111 (not_111_out, op5);
  not not_112 (not_112_out, op4);
  not not_113 (not_113_out, op2);
  not not_114 (not_114_out, op1);
  not not_115 (not_115_out, op5);
  not not_116 (not_116_out, op4);
  not not_117 (not_117_out, op1);
  not not_118 (not_118_out, op0);
  not not_119 (not_119_out, op4);
  not not_120 (not_120_out, op3);
  not not_121 (not_121_out, op2);
  not not_122 (not_122_out, op4);
  not not_123 (not_123_out, op2);
  not not_124 (not_124_out, op5);
  not not_125 (not_125_out, op4);
  not not_126 (not_126_out, op3);
  not not_127 (not_127_out, op2);
  not not_128 (not_128_out, op1);
  not not_129 (not_129_out, op0);
  not not_130 (not_130_out, f4);
  not not_131 (not_131_out, f3);
  not not_132 (not_132_out, f2);
  not not_133 (not_133_out, f1);
  not not_134 (not_134_out, f0);
  not not_135 (not_135_out, op5);
  not not_136 (not_136_out, op4);
  not not_137 (not_137_out, op3);
  not not_138 (not_138_out, op2);
  not not_139 (not_139_out, op1);
  not not_140 (not_140_out, op0);
  not not_141 (not_141_out, f4);
  not not_142 (not_142_out, f3);
  not not_143 (not_143_out, f2);
  not not_144 (not_144_out, f1);
  not not_145 (not_145_out, op5);
  not not_146 (not_146_out, op4);
  not not_147 (not_147_out, op3);
  not not_148 (not_148_out, op2);
  not not_149 (not_149_out, op1);
  not not_150 (not_150_out, op0);
  not not_151 (not_151_out, f4);
  not not_152 (not_152_out, f3);
  not not_153 (not_153_out, f1);
  not not_154 (not_154_out, f0);
  not not_155 (not_155_out, op5);
  not not_156 (not_156_out, op4);
  not not_157 (not_157_out, op3);
  not not_158 (not_158_out, op2);
  not not_159 (not_159_out, op1);
  not not_160 (not_160_out, op0);
  not not_161 (not_161_out, f4);
  not not_162 (not_162_out, f3);
  not not_163 (not_163_out, f2);
  not not_164 (not_164_out, f0);
  not not_165 (not_165_out, op5);
  not not_166 (not_166_out, op4);
  not not_167 (not_167_out, op3);
  not not_168 (not_168_out, op2);
  not not_169 (not_169_out, op1);
  not not_170 (not_170_out, op0);
  not not_171 (not_171_out, f4);
  not not_172 (not_172_out, f2);
  not not_173 (not_173_out, op4);
  not not_174 (not_174_out, op3);
  not not_175 (not_175_out, op2);
  not not_176 (not_176_out, op1);
  not not_177 (not_177_out, op4);
  not not_178 (not_178_out, op2);
  not not_179 (not_179_out, op1);
  not not_180 (not_180_out, op0);
  not not_181 (not_181_out, op5);
  not not_182 (not_182_out, op4);
  not not_183 (not_183_out, op1);
  not not_184 (not_184_out, op0);
  not not_185 (not_185_out, op5);
  not not_186 (not_186_out, op4);
  not not_187 (not_187_out, op2);
  not not_188 (not_188_out, op0);
  not not_189 (not_189_out, op5);
  not not_190 (not_190_out, op4);
  not not_191 (not_191_out, op3);
  not not_192 (not_192_out, op2);
  not not_193 (not_193_out, op1);
  not not_194 (not_194_out, op0);
  not not_195 (not_195_out, f4);
  not not_196 (not_196_out, f3);
  not not_197 (not_197_out, f1);
  not not_198 (not_198_out, f0);
  not not_199 (not_199_out, op5);
  not not_200 (not_200_out, op4);
  not not_201 (not_201_out, op3);
  not not_202 (not_202_out, op2);
  not not_203 (not_203_out, op1);
  not not_204 (not_204_out, op0);
  not not_205 (not_205_out, f5);
  not not_206 (not_206_out, f4);
  not not_207 (not_207_out, f3);
  not not_208 (not_208_out, f2);
  not not_209 (not_209_out, f0);
  not not_210 (not_210_out, op5);
  not not_211 (not_211_out, op4);
  not not_212 (not_212_out, op3);
  not not_213 (not_213_out, op2);
  not not_214 (not_214_out, op1);
  not not_215 (not_215_out, op0);
  not not_216 (not_216_out, f4);
  not not_217 (not_217_out, f3);
  not not_218 (not_218_out, f2);
  not not_219 (not_219_out, f0);
  not not_220 (not_220_out, op5);
  not not_221 (not_221_out, op4);
  not not_222 (not_222_out, op3);
  not not_223 (not_223_out, op2);
  not not_224 (not_224_out, op1);
  not not_225 (not_225_out, op0);
  not not_226 (not_226_out, f4);
  not not_227 (not_227_out, f3);
  not not_228 (not_228_out, op5);
  not not_229 (not_229_out, op4);
  not not_230 (not_230_out, op3);
  not not_231 (not_231_out, op2);
  not not_232 (not_232_out, op1);
  not not_233 (not_233_out, op0);
  not not_234 (not_234_out, f4);
  not not_235 (not_235_out, f2);
  not not_236 (not_236_out, f0);
  not not_237 (not_237_out, op5);
  not not_238 (not_238_out, op4);
  not not_239 (not_239_out, op2);
  not not_240 (not_240_out, op1);
  not not_241 (not_241_out, op0);
  not not_242 (not_242_out, op5);
  not not_243 (not_243_out, op4);
  not not_244 (not_244_out, op2);
  not not_245 (not_245_out, op1);
  not not_246 (not_246_out, op5);
  not not_247 (not_247_out, op4);
  not not_248 (not_248_out, op1);
  not not_249 (not_249_out, op0);
  not not_250 (not_250_out, op4);
  not not_251 (not_251_out, op3);
  not not_252 (not_252_out, op2);
  not not_253 (not_253_out, op4);
  not not_254 (not_254_out, op2);
  not not_255 (not_255_out, op5);
  not not_256 (not_256_out, op4);
  not not_257 (not_257_out, op2);
  not not_258 (not_258_out, op0);
  not not_259 (not_259_out, op5);
  not not_260 (not_260_out, op4);
  not not_261 (not_261_out, op3);
  not not_262 (not_262_out, op2);
  not not_263 (not_263_out, op1);
  not not_264 (not_264_out, op0);
  not not_265 (not_265_out, f4);
  not not_266 (not_266_out, f3);
  not not_267 (not_267_out, f2);
  not not_268 (not_268_out, f1);
  not not_269 (not_269_out, f0);
  not not_270 (not_270_out, op5);
  not not_271 (not_271_out, op4);
  not not_272 (not_272_out, op3);
  not not_273 (not_273_out, op2);
  not not_274 (not_274_out, op1);
  not not_275 (not_275_out, op0);
  not not_276 (not_276_out, f4);
  not not_277 (not_277_out, f3);
  not not_278 (not_278_out, f2);
  not not_279 (not_279_out, f1);
  not not_280 (not_280_out, op5);
  not not_281 (not_281_out, op4);
  not not_282 (not_282_out, op3);
  not not_283 (not_283_out, op2);
  not not_284 (not_284_out, op1);
  not not_285 (not_285_out, op0);
  not not_286 (not_286_out, f4);
  not not_287 (not_287_out, f3);
  not not_288 (not_288_out, f1);
  not not_289 (not_289_out, f0);
  not not_290 (not_290_out, op5);
  not not_291 (not_291_out, op4);
  not not_292 (not_292_out, op3);
  not not_293 (not_293_out, op2);
  not not_294 (not_294_out, op1);
  not not_295 (not_295_out, op0);
  not not_296 (not_296_out, f5);
  not not_297 (not_297_out, f4);
  not not_298 (not_298_out, f3);
  not not_299 (not_299_out, f2);
  not not_300 (not_300_out, op5);
  not not_301 (not_301_out, op4);
  not not_302 (not_302_out, op3);
  not not_303 (not_303_out, op2);
  not not_304 (not_304_out, op1);
  not not_305 (not_305_out, op0);
  not not_306 (not_306_out, f4);
  not not_307 (not_307_out, f2);
  not not_308 (not_308_out, f0);
  not not_309 (not_309_out, op5);
  not not_310 (not_310_out, op4);
  not not_311 (not_311_out, op3);
  not not_312 (not_312_out, op2);
  not not_313 (not_313_out, op1);
  not not_314 (not_314_out, op0);
  not not_315 (not_315_out, f5);
  not not_316 (not_316_out, f4);
  not not_317 (not_317_out, f3);
  not not_318 (not_318_out, op4);
  not not_319 (not_319_out, op3);
  not not_320 (not_320_out, op2);
  not not_321 (not_321_out, op1);
  not not_322 (not_322_out, op4);
  not not_323 (not_323_out, op2);
  not not_324 (not_324_out, op1);
  not not_325 (not_325_out, op0);
  not not_326 (not_326_out, op5);
  not not_327 (not_327_out, op4);
  not not_328 (not_328_out, op3);
  not not_329 (not_329_out, op2);
  not not_330 (not_330_out, op1);
  not not_331 (not_331_out, op0);
  not not_332 (not_332_out, f5);
  not not_333 (not_333_out, f4);
  not not_334 (not_334_out, f1);
  not not_335 (not_335_out, f0);
  not not_336 (not_336_out, op5);
  not not_337 (not_337_out, op4);
  not not_338 (not_338_out, op3);
  not not_339 (not_339_out, op2);
  not not_340 (not_340_out, op1);
  not not_341 (not_341_out, op0);
  not not_342 (not_342_out, f5);
  not not_343 (not_343_out, f4);
  not not_344 (not_344_out, f3);
  not not_345 (not_345_out, op5);
  not not_346 (not_346_out, op4);
  not not_347 (not_347_out, op4);
  not not_348 (not_348_out, op2);
  not not_349 (not_349_out, op1);
  not not_350 (not_350_out, op0);
  not not_351 (not_351_out, op5);
  not not_352 (not_352_out, op4);
  not not_353 (not_353_out, op3);
  and and_1 (and_1_out, not_1_out, not_2_out, op3, not_3_out, not_4_out, not_5_out);
  and and_2 (and_2_out, not_6_out, not_7_out, op3, not_8_out, not_9_out, op0);
  and and_3 (and_3_out, not_10_out, not_11_out, op3, op2, not_12_out, not_13_out);
  and and_4 (and_4_out, not_14_out, not_15_out, op3, op2, not_16_out, op0);
  and and_5 (and_5_out, op5, not_17_out, not_18_out, not_19_out, op1, op0);
  and and_6 (and_6_out, op5, not_20_out, op3, not_21_out, op1, op0);
  and and_7 (and_7_out, not_22_out, not_23_out, op3, not_24_out, op1, not_25_out);
  and and_8 (and_8_out, not_26_out, not_27_out, not_28_out, not_29_out, not_30_out, not_31_out, not_32_out, not_33_out, not_34_out, not_35_out, not_36_out, not_37_out);
  and and_9 (and_9_out, not_38_out, not_39_out, not_40_out, not_41_out, not_42_out, not_43_out, not_44_out, not_45_out, not_46_out, not_47_out, f1, f0);
  and and_10 (and_10_out, not_48_out, not_49_out, not_50_out, not_51_out, not_52_out, not_53_out, not_54_out, not_55_out, not_56_out, not_57_out, f1, not_58_out);
  and and_11 (and_11_out, not_59_out, not_60_out, op3, op2, op1, op0);
  and and_12 (and_12_out, op5, not_61_out, op3, not_62_out, not_63_out, not_64_out);
  and and_13 (and_13_out, not_65_out, not_66_out, op3, op2, not_67_out, op0);
  and and_14 (and_14_out, not_68_out, not_69_out, op3, not_70_out, op1, not_71_out);
  and and_15 (and_15_out, not_72_out, not_73_out, not_74_out, not_75_out, not_76_out, not_77_out, f5, not_78_out, not_79_out, f2, not_80_out, f0);
  and and_16 (and_16_out, not_81_out, not_82_out, not_83_out, not_84_out, not_85_out, not_86_out, f5, not_87_out, not_88_out, f2, f1, f0);
  and and_17 (and_17_out, not_89_out, not_90_out, not_91_out, not_92_out, not_93_out, not_94_out, f5, not_95_out, f3, not_96_out, f1, not_97_out);
  and and_18 (and_18_out, not_98_out, not_99_out, not_100_out, not_101_out, not_102_out, not_103_out, f5, not_104_out, f3, not_105_out, f1, f0);
  and and_19 (and_19_out, not_106_out, not_107_out, op3, not_108_out, not_109_out, not_110_out);
  and and_20 (and_20_out, not_111_out, not_112_out, op3, not_113_out, not_114_out, op0);
  and and_21 (and_21_out, not_115_out, not_116_out, op3, op2, not_117_out, not_118_out);
  and and_22 (and_22_out, op5, not_119_out, not_120_out, not_121_out, op1, op0);
  and and_23 (and_23_out, op5, not_122_out, op3, not_123_out, op1, op0);
  and and_24 (and_24_out, not_124_out, not_125_out, not_126_out, not_127_out, not_128_out, not_129_out, f5, not_130_out, not_131_out, not_132_out, not_133_out, not_134_out);
  and and_25 (and_25_out, not_135_out, not_136_out, not_137_out, not_138_out, not_139_out, not_140_out, f5, not_141_out, not_142_out, not_143_out, not_144_out, f0);
  and and_26 (and_26_out, not_145_out, not_146_out, not_147_out, not_148_out, not_149_out, not_150_out, f5, not_151_out, not_152_out, f2, not_153_out, not_154_out);
  and and_27 (and_27_out, not_155_out, not_156_out, not_157_out, not_158_out, not_159_out, not_160_out, f5, not_161_out, not_162_out, not_163_out, f1, not_164_out);
  and and_28 (and_28_out, not_165_out, not_166_out, not_167_out, not_168_out, not_169_out, not_170_out, f5, not_171_out, f3, not_172_out, f1, f0);
  and and_29 (and_29_out, op5, not_173_out, not_174_out, not_175_out, not_176_out, op0);
  and and_30 (and_30_out, op5, not_177_out, op3, not_178_out, not_179_out, not_180_out);
  and and_31 (and_31_out, not_181_out, not_182_out, op3, op2, not_183_out, not_184_out);
  and and_32 (and_32_out, not_185_out, not_186_out, op3, not_187_out, op1, not_188_out);
  and and_33 (and_33_out, not_189_out, not_190_out, not_191_out, not_192_out, not_193_out, not_194_out, f5, not_195_out, not_196_out, f2, not_197_out, not_198_out);
  and and_34 (and_34_out, not_199_out, not_200_out, not_201_out, not_202_out, not_203_out, not_204_out, not_205_out, not_206_out, not_207_out, not_208_out, f1, not_209_out);
  and and_35 (and_35_out, not_210_out, not_211_out, not_212_out, not_213_out, not_214_out, not_215_out, f5, not_216_out, not_217_out, not_218_out, f1, not_219_out);
  and and_36 (and_36_out, not_220_out, not_221_out, not_222_out, not_223_out, not_224_out, not_225_out, f5, not_226_out, not_227_out, f2, f1, f0);
  and and_37 (and_37_out, not_228_out, not_229_out, not_230_out, not_231_out, not_232_out, not_233_out, f5, not_234_out, f3, not_235_out, f1, not_236_out);
  and and_38 (and_38_out, not_237_out, not_238_out, op3, not_239_out, not_240_out, not_241_out);
  and and_39 (and_39_out, not_242_out, not_243_out, op3, not_244_out, not_245_out, op0);
  and and_40 (and_40_out, not_246_out, not_247_out, op3, op2, not_248_out, not_249_out);
  and and_41 (and_41_out, op5, not_250_out, not_251_out, not_252_out, op1, op0);
  and and_42 (and_42_out, op5, not_253_out, op3, not_254_out, op1, op0);
  and and_43 (and_43_out, not_255_out, not_256_out, op3, not_257_out, op1, not_258_out);
  and and_44 (and_44_out, not_259_out, not_260_out, not_261_out, not_262_out, not_263_out, not_264_out, f5, not_265_out, not_266_out, not_267_out, not_268_out, not_269_out);
  and and_45 (and_45_out, not_270_out, not_271_out, not_272_out, not_273_out, not_274_out, not_275_out, f5, not_276_out, not_277_out, not_278_out, not_279_out, f0);
  and and_46 (and_46_out, not_280_out, not_281_out, not_282_out, not_283_out, not_284_out, not_285_out, f5, not_286_out, not_287_out, f2, not_288_out, not_289_out);
  and and_47 (and_47_out, not_290_out, not_291_out, not_292_out, not_293_out, not_294_out, not_295_out, not_296_out, not_297_out, not_298_out, not_299_out, f1, f0);
  and and_48 (and_48_out, not_300_out, not_301_out, not_302_out, not_303_out, not_304_out, not_305_out, f5, not_306_out, f3, not_307_out, f1, not_308_out);
  and and_49 (and_49_out, not_309_out, not_310_out, not_311_out, not_312_out, not_313_out, not_314_out, not_315_out, not_316_out, not_317_out, f2, f1, f0);
  and and_50 (and_50_out, op5, not_318_out, not_319_out, not_320_out, not_321_out, op0);
  and and_51 (and_51_out, op5, not_322_out, op3, not_323_out, not_324_out, not_325_out);
  and and_52 (sys, not_326_out, not_327_out, not_328_out, not_329_out, not_330_out, not_331_out, not_332_out, not_333_out, f3, f2, not_334_out, not_335_out);
  and and_53 (srav, not_336_out, not_337_out, not_338_out, not_339_out, not_340_out, not_341_out, not_342_out, not_343_out, not_344_out, f2, f1, f0);
  and and_54 (lui, not_345_out, not_346_out, op3, op2, op1, op0);
  and and_55 (sb, op5, not_347_out, op3, not_348_out, not_349_out, not_350_out);
  and and_56 (bgtz, not_351_out, not_352_out, not_353_out, op2, op1, op0);
  or or_1 (AluCtrl3, and_13_out, and_14_out, and_15_out, and_16_out, and_17_out, and_18_out);
  or or_2 (AluCtrl1, and_31_out, and_32_out, and_33_out, and_34_out, and_35_out, and_36_out, and_37_out);
  or or_3 (AluSrc, and_1_out, and_2_out, and_3_out, and_4_out, and_5_out, and_6_out, and_7_out, and_8_out, and_9_out, and_10_out, and_11_out, and_12_out);
  or or_4 (AluCtrl2, and_19_out, and_20_out, and_21_out, and_22_out, and_23_out, and_24_out, and_25_out, and_26_out, and_27_out, and_28_out, and_29_out, and_30_out);
  or or_5 (AluCtrl0, and_38_out, and_39_out, and_40_out, and_41_out, and_42_out, and_43_out, and_44_out, and_45_out, and_46_out, and_47_out, and_48_out, and_49_out, and_50_out, and_51_out);
endmodule

module \控制器  (
  input  op5,
  input  op4,
  input  op3,
  input  op2,
  input  op1,
  input  op0,
  input  f5,
  input  f4,
  input  f3,
  input  f2,
  input  f1,
  input  f0,
  output Zeroextend,
  output RegDst,
  output Shift,
  output j,
  output jal,
  output jr,
  output beq,
  output bne,
  output MemRead,
  output MemtoReg,
  output MemWrite,
  output RegWrite
);

  wire and_1_out, and_2_out, and_3_out, and_5_out, and_6_out, and_7_out, and_14_out, and_15_out, and_16_out,
       and_17_out, and_18_out, and_19_out, and_20_out, and_21_out, and_22_out, and_23_out, and_24_out,
       and_25_out, and_26_out, and_27_out, and_28_out, and_29_out, and_30_out, and_31_out, and_32_out,
       and_33_out, and_34_out, and_35_out, and_36_out, and_37_out, not_1_out, not_2_out, not_3_out,
       not_4_out, not_5_out, not_6_out, not_7_out, not_8_out, not_9_out, not_10_out, not_11_out, not_12_out,
       not_13_out, not_14_out, not_15_out, not_16_out, not_17_out, not_18_out, not_19_out, not_20_out,
       not_21_out, not_22_out, not_23_out, not_24_out, not_25_out, not_26_out, not_27_out, not_28_out,
       not_29_out, not_30_out, not_31_out, not_32_out, not_33_out, not_34_out, not_35_out, not_36_out,
       not_37_out, not_38_out, not_39_out, not_40_out, not_41_out, not_42_out, not_43_out, not_44_out,
       not_45_out, not_46_out, not_47_out, not_48_out, not_49_out, not_50_out, not_51_out, not_52_out,
       not_53_out, not_54_out, not_55_out, not_56_out, not_57_out, not_58_out, not_59_out, not_60_out,
       not_61_out, not_62_out, not_63_out, not_64_out, not_65_out, not_66_out, not_67_out, not_68_out,
       not_69_out, not_70_out, not_71_out, not_72_out, not_73_out, not_74_out, not_75_out, not_76_out,
       not_77_out, not_78_out, not_79_out, not_80_out, not_81_out, not_82_out, not_83_out, not_84_out,
       not_85_out, not_86_out, not_87_out, not_88_out, not_89_out, not_90_out, not_91_out, not_92_out,
       not_93_out, not_94_out, not_95_out, not_96_out, not_97_out, not_98_out, not_99_out, not_100_out,
       not_101_out, not_102_out, not_103_out, not_104_out, not_105_out, not_106_out, not_107_out,
       not_108_out, not_109_out, not_110_out, not_111_out, not_112_out, not_113_out, not_114_out,
       not_115_out, not_116_out, not_117_out, not_118_out, not_119_out, not_120_out, not_121_out,
       not_122_out, not_123_out, not_124_out, not_125_out, not_126_out, not_127_out, not_128_out,
       not_129_out, not_130_out, not_131_out, not_132_out, not_133_out, not_134_out, not_135_out,
       not_136_out, not_137_out, not_138_out, not_139_out, not_140_out, not_141_out, not_142_out,
       not_143_out, not_144_out, not_145_out, not_146_out, not_147_out, not_148_out, not_149_out,
       not_150_out, not_151_out, not_152_out, not_153_out, not_154_out, not_155_out, not_156_out,
       not_157_out, not_158_out, not_159_out, not_160_out, not_161_out, not_162_out, not_163_out,
       not_164_out, not_165_out, not_166_out, not_167_out, not_168_out, not_169_out, not_170_out,
       not_171_out, not_172_out, not_173_out, not_174_out, not_175_out, not_176_out, not_177_out,
       not_178_out, not_179_out, not_180_out, not_181_out, not_182_out, not_183_out, not_184_out,
       not_185_out, not_186_out, not_187_out, not_188_out, not_189_out, not_190_out, not_191_out,
       not_192_out, not_193_out, not_194_out, not_195_out, not_196_out, not_197_out, not_198_out,
       not_199_out, not_200_out, not_201_out, not_202_out, not_203_out, not_204_out, not_205_out,
       not_206_out, not_207_out, not_208_out, not_209_out, not_210_out, not_211_out, not_212_out,
       not_213_out, not_214_out, not_215_out, not_216_out, not_217_out, not_218_out, not_219_out,
       not_220_out, not_221_out, not_222_out, not_223_out, not_224_out, not_225_out, not_226_out,
       not_227_out, not_228_out, not_229_out, not_230_out, not_231_out, not_232_out, not_233_out,
       not_234_out, not_235_out, not_236_out, not_237_out, not_238_out, not_239_out, not_240_out,
       not_241_out, not_242_out, not_243_out, not_244_out, not_245_out, not_246_out;

  not not_1 (not_1_out, op5);
  not not_2 (not_2_out, op4);
  not not_3 (not_3_out, op1);
  not not_4 (not_4_out, op0);
  not not_5 (not_5_out, op5);
  not not_6 (not_6_out, op4);
  not not_7 (not_7_out, op1);
  not not_8 (not_8_out, op5);
  not not_9 (not_9_out, op4);
  not not_10 (not_10_out, op2);
  not not_11 (not_11_out, op1);
  not not_12 (not_12_out, op5);
  not not_13 (not_13_out, op4);
  not not_14 (not_14_out, op4);
  not not_15 (not_15_out, op3);
  not not_16 (not_16_out, op2);
  not not_17 (not_17_out, op1);
  not not_18 (not_18_out, op0);
  not not_19 (not_19_out, op5);
  not not_20 (not_20_out, op4);
  not not_21 (not_21_out, op4);
  not not_22 (not_22_out, op3);
  not not_23 (not_23_out, op2);
  not not_24 (not_24_out, op1);
  not not_25 (not_25_out, op0);
  not not_26 (not_26_out, f5);
  not not_27 (not_27_out, f4);
  not not_28 (not_28_out, f3);
  not not_29 (not_29_out, f2);
  not not_30 (not_30_out, f1);
  not not_31 (not_31_out, f0);
  not not_32 (not_32_out, op5);
  not not_33 (not_33_out, op4);
  not not_34 (not_34_out, op4);
  not not_35 (not_35_out, op3);
  not not_36 (not_36_out, op2);
  not not_37 (not_37_out, op1);
  not not_38 (not_38_out, op0);
  not not_39 (not_39_out, f5);
  not not_40 (not_40_out, f4);
  not not_41 (not_41_out, f3);
  not not_42 (not_42_out, f2);
  not not_43 (not_43_out, op5);
  not not_44 (not_44_out, op4);
  not not_45 (not_45_out, op4);
  not not_46 (not_46_out, op3);
  not not_47 (not_47_out, op2);
  not not_48 (not_48_out, op1);
  not not_49 (not_49_out, op0);
  not not_50 (not_50_out, f5);
  not not_51 (not_51_out, f4);
  not not_52 (not_52_out, f3);
  not not_53 (not_53_out, f2);
  not not_54 (not_54_out, f0);
  not not_55 (not_55_out, op5);
  not not_56 (not_56_out, op4);
  not not_57 (not_57_out, op3);
  not not_58 (not_58_out, op2);
  not not_59 (not_59_out, op0);
  not not_60 (not_60_out, op5);
  not not_61 (not_61_out, op4);
  not not_62 (not_62_out, op3);
  not not_63 (not_63_out, op2);
  not not_64 (not_64_out, op5);
  not not_65 (not_65_out, op4);
  not not_66 (not_66_out, op4);
  not not_67 (not_67_out, op3);
  not not_68 (not_68_out, op2);
  not not_69 (not_69_out, op1);
  not not_70 (not_70_out, op0);
  not not_71 (not_71_out, f5);
  not not_72 (not_72_out, f4);
  not not_73 (not_73_out, f2);
  not not_74 (not_74_out, f1);
  not not_75 (not_75_out, f0);
  not not_76 (not_76_out, op5);
  not not_77 (not_77_out, op4);
  not not_78 (not_78_out, op3);
  not not_79 (not_79_out, op1);
  not not_80 (not_80_out, op0);
  not not_81 (not_81_out, op5);
  not not_82 (not_82_out, op4);
  not not_83 (not_83_out, op3);
  not not_84 (not_84_out, op1);
  not not_85 (not_85_out, op4);
  not not_86 (not_86_out, op3);
  not not_87 (not_87_out, op2);
  not not_88 (not_88_out, op4);
  not not_89 (not_89_out, op3);
  not not_90 (not_90_out, op2);
  not not_91 (not_91_out, op4);
  not not_92 (not_92_out, op3);
  not not_93 (not_93_out, op2);
  not not_94 (not_94_out, op1);
  not not_95 (not_95_out, op4);
  not not_96 (not_96_out, op2);
  not not_97 (not_97_out, op4);
  not not_98 (not_98_out, op2);
  not not_99 (not_99_out, op1);
  not not_100 (not_100_out, op0);
  not not_101 (not_101_out, op5);
  not not_102 (not_102_out, op4);
  not not_103 (not_103_out, op2);
  not not_104 (not_104_out, op1);
  not not_105 (not_105_out, op0);
  not not_106 (not_106_out, op5);
  not not_107 (not_107_out, op4);
  not not_108 (not_108_out, op2);
  not not_109 (not_109_out, op1);
  not not_110 (not_110_out, op5);
  not not_111 (not_111_out, op4);
  not not_112 (not_112_out, op1);
  not not_113 (not_113_out, op0);
  not not_114 (not_114_out, op5);
  not not_115 (not_115_out, op4);
  not not_116 (not_116_out, op1);
  not not_117 (not_117_out, op4);
  not not_118 (not_118_out, op3);
  not not_119 (not_119_out, op2);
  not not_120 (not_120_out, op5);
  not not_121 (not_121_out, op4);
  not not_122 (not_122_out, op2);
  not not_123 (not_123_out, op0);
  not not_124 (not_124_out, op5);
  not not_125 (not_125_out, op4);
  not not_126 (not_126_out, op3);
  not not_127 (not_127_out, op2);
  not not_128 (not_128_out, op5);
  not not_129 (not_129_out, op4);
  not not_130 (not_130_out, op3);
  not not_131 (not_131_out, op2);
  not not_132 (not_132_out, op1);
  not not_133 (not_133_out, op0);
  not not_134 (not_134_out, f4);
  not not_135 (not_135_out, f3);
  not not_136 (not_136_out, f2);
  not not_137 (not_137_out, f1);
  not not_138 (not_138_out, f0);
  not not_139 (not_139_out, op5);
  not not_140 (not_140_out, op4);
  not not_141 (not_141_out, op3);
  not not_142 (not_142_out, op2);
  not not_143 (not_143_out, op1);
  not not_144 (not_144_out, op0);
  not not_145 (not_145_out, f4);
  not not_146 (not_146_out, f3);
  not not_147 (not_147_out, f2);
  not not_148 (not_148_out, f1);
  not not_149 (not_149_out, op5);
  not not_150 (not_150_out, op4);
  not not_151 (not_151_out, op3);
  not not_152 (not_152_out, op2);
  not not_153 (not_153_out, op1);
  not not_154 (not_154_out, op0);
  not not_155 (not_155_out, f4);
  not not_156 (not_156_out, f3);
  not not_157 (not_157_out, f1);
  not not_158 (not_158_out, f0);
  not not_159 (not_159_out, op5);
  not not_160 (not_160_out, op4);
  not not_161 (not_161_out, op3);
  not not_162 (not_162_out, op2);
  not not_163 (not_163_out, op1);
  not not_164 (not_164_out, op0);
  not not_165 (not_165_out, f5);
  not not_166 (not_166_out, f4);
  not not_167 (not_167_out, f3);
  not not_168 (not_168_out, f2);
  not not_169 (not_169_out, f1);
  not not_170 (not_170_out, f0);
  not not_171 (not_171_out, op5);
  not not_172 (not_172_out, op4);
  not not_173 (not_173_out, op3);
  not not_174 (not_174_out, op2);
  not not_175 (not_175_out, op1);
  not not_176 (not_176_out, op0);
  not not_177 (not_177_out, f5);
  not not_178 (not_178_out, f4);
  not not_179 (not_179_out, f3);
  not not_180 (not_180_out, f2);
  not not_181 (not_181_out, op5);
  not not_182 (not_182_out, op4);
  not not_183 (not_183_out, op3);
  not not_184 (not_184_out, op2);
  not not_185 (not_185_out, op1);
  not not_186 (not_186_out, op0);
  not not_187 (not_187_out, f5);
  not not_188 (not_188_out, f4);
  not not_189 (not_189_out, f3);
  not not_190 (not_190_out, f2);
  not not_191 (not_191_out, f0);
  not not_192 (not_192_out, op5);
  not not_193 (not_193_out, op4);
  not not_194 (not_194_out, op3);
  not not_195 (not_195_out, op2);
  not not_196 (not_196_out, op1);
  not not_197 (not_197_out, op0);
  not not_198 (not_198_out, f4);
  not not_199 (not_199_out, f3);
  not not_200 (not_200_out, f2);
  not not_201 (not_201_out, f0);
  not not_202 (not_202_out, op5);
  not not_203 (not_203_out, op4);
  not not_204 (not_204_out, op3);
  not not_205 (not_205_out, op2);
  not not_206 (not_206_out, op1);
  not not_207 (not_207_out, op0);
  not not_208 (not_208_out, f4);
  not not_209 (not_209_out, f3);
  not not_210 (not_210_out, f1);
  not not_211 (not_211_out, op5);
  not not_212 (not_212_out, op4);
  not not_213 (not_213_out, op3);
  not not_214 (not_214_out, op2);
  not not_215 (not_215_out, op1);
  not not_216 (not_216_out, op0);
  not not_217 (not_217_out, f4);
  not not_218 (not_218_out, f3);
  not not_219 (not_219_out, op5);
  not not_220 (not_220_out, op4);
  not not_221 (not_221_out, op3);
  not not_222 (not_222_out, op2);
  not not_223 (not_223_out, op1);
  not not_224 (not_224_out, op0);
  not not_225 (not_225_out, f4);
  not not_226 (not_226_out, f2);
  not not_227 (not_227_out, f0);
  not not_228 (not_228_out, op5);
  not not_229 (not_229_out, op4);
  not not_230 (not_230_out, op3);
  not not_231 (not_231_out, op2);
  not not_232 (not_232_out, op1);
  not not_233 (not_233_out, op0);
  not not_234 (not_234_out, f4);
  not not_235 (not_235_out, f2);
  not not_236 (not_236_out, op5);
  not not_237 (not_237_out, op4);
  not not_238 (not_238_out, op3);
  not not_239 (not_239_out, op2);
  not not_240 (not_240_out, op1);
  not not_241 (not_241_out, op0);
  not not_242 (not_242_out, f5);
  not not_243 (not_243_out, f4);
  not not_244 (not_244_out, f3);
  not not_245 (not_245_out, op5);
  not not_246 (not_246_out, op4);
  and and_1 (and_1_out, not_1_out, not_2_out, op3, op2, not_3_out, not_4_out);
  and and_2 (and_2_out, not_5_out, not_6_out, op3, op2, not_7_out, op0);
  and and_3 (and_3_out, not_8_out, not_9_out, op3, not_10_out, not_11_out, op0);
  and and_4 (RegDst, not_12_out, not_13_out, not_14_out, not_15_out, not_16_out, not_17_out, not_18_out);
  and and_5 (and_5_out, not_19_out, not_20_out, not_21_out, not_22_out, not_23_out, not_24_out, not_25_out, not_26_out, not_27_out, not_28_out, not_29_out, not_30_out, not_31_out);
  and and_6 (and_6_out, not_32_out, not_33_out, not_34_out, not_35_out, not_36_out, not_37_out, not_38_out, not_39_out, not_40_out, not_41_out, not_42_out, f1, f0);
  and and_7 (and_7_out, not_43_out, not_44_out, not_45_out, not_46_out, not_47_out, not_48_out, not_49_out, not_50_out, not_51_out, not_52_out, not_53_out, f1, not_54_out);
  and and_8 (j, not_55_out, not_56_out, not_57_out, not_58_out, op1, not_59_out);
  and and_9 (jal, not_60_out, not_61_out, not_62_out, not_63_out, op1, op0);
  and and_10 (jr, not_64_out, not_65_out, not_66_out, not_67_out, not_68_out, not_69_out, not_70_out, not_71_out, not_72_out, f3, not_73_out, not_74_out, not_75_out);
  and and_11 (beq, not_76_out, not_77_out, not_78_out, op2, not_79_out, not_80_out);
  and and_12 (bne, not_81_out, not_82_out, not_83_out, op2, not_84_out, op0);
  and and_13 (MemRead, op5, not_85_out, not_86_out, not_87_out, op1, op0);
  and and_14 (and_14_out, op5, not_88_out, not_89_out, not_90_out, op1, op0);
  and and_15 (and_15_out, op5, not_91_out, not_92_out, not_93_out, not_94_out, op0);
  and and_16 (and_16_out, op5, not_95_out, op3, not_96_out, op1, op0);
  and and_17 (and_17_out, op5, not_97_out, op3, not_98_out, not_99_out, not_100_out);
  and and_18 (and_18_out, not_101_out, not_102_out, op3, not_103_out, not_104_out, not_105_out);
  and and_19 (and_19_out, not_106_out, not_107_out, op3, not_108_out, not_109_out, op0);
  and and_20 (and_20_out, not_110_out, not_111_out, op3, op2, not_112_out, not_113_out);
  and and_21 (and_21_out, not_114_out, not_115_out, op3, op2, not_116_out, op0);
  and and_22 (and_22_out, op5, not_117_out, not_118_out, not_119_out, op1, op0);
  and and_23 (and_23_out, not_120_out, not_121_out, op3, not_122_out, op1, not_123_out);
  and and_24 (and_24_out, not_124_out, not_125_out, not_126_out, not_127_out, op1, op0);
  and and_25 (and_25_out, not_128_out, not_129_out, not_130_out, not_131_out, not_132_out, not_133_out, f5, not_134_out, not_135_out, not_136_out, not_137_out, not_138_out);
  and and_26 (and_26_out, not_139_out, not_140_out, not_141_out, not_142_out, not_143_out, not_144_out, f5, not_145_out, not_146_out, not_147_out, not_148_out, f0);
  and and_27 (and_27_out, not_149_out, not_150_out, not_151_out, not_152_out, not_153_out, not_154_out, f5, not_155_out, not_156_out, f2, not_157_out, not_158_out);
  and and_28 (and_28_out, not_159_out, not_160_out, not_161_out, not_162_out, not_163_out, not_164_out, not_165_out, not_166_out, not_167_out, not_168_out, not_169_out, not_170_out);
  and and_29 (and_29_out, not_171_out, not_172_out, not_173_out, not_174_out, not_175_out, not_176_out, not_177_out, not_178_out, not_179_out, not_180_out, f1, f0);
  and and_30 (and_30_out, not_181_out, not_182_out, not_183_out, not_184_out, not_185_out, not_186_out, not_187_out, not_188_out, not_189_out, not_190_out, f1, not_191_out);
  and and_31 (and_31_out, not_192_out, not_193_out, not_194_out, not_195_out, not_196_out, not_197_out, f5, not_198_out, not_199_out, not_200_out, f1, not_201_out);
  and and_32 (and_32_out, not_202_out, not_203_out, not_204_out, not_205_out, not_206_out, not_207_out, f5, not_208_out, not_209_out, f2, not_210_out, f0);
  and and_33 (and_33_out, not_211_out, not_212_out, not_213_out, not_214_out, not_215_out, not_216_out, f5, not_217_out, not_218_out, f2, f1, f0);
  and and_34 (and_34_out, not_219_out, not_220_out, not_221_out, not_222_out, not_223_out, not_224_out, f5, not_225_out, f3, not_226_out, f1, not_227_out);
  and and_35 (and_35_out, not_228_out, not_229_out, not_230_out, not_231_out, not_232_out, not_233_out, f5, not_234_out, f3, not_235_out, f1, f0);
  and and_36 (and_36_out, not_236_out, not_237_out, not_238_out, not_239_out, not_240_out, not_241_out, not_242_out, not_243_out, not_244_out, f2, f1, f0);
  and and_37 (and_37_out, not_245_out, not_246_out, op3, op2, op1, op0);
  or or_1 (Zeroextend, and_1_out, and_2_out, and_3_out);
  or or_2 (Shift, and_5_out, and_6_out, and_7_out);
  or or_3 (MemtoReg, and_14_out, and_15_out);
  or or_4 (MemWrite, and_16_out, and_17_out);
  or or_5 (RegWrite, and_18_out, and_19_out, and_20_out, and_21_out, and_22_out, and_23_out, and_24_out, and_25_out, and_26_out, and_27_out, and_28_out, and_29_out, and_30_out, and_31_out, and_32_out, and_33_out, and_34_out, and_35_out, and_36_out, and_37_out);
endmodule

module \中断  (
  input  clk,
  input  IR1,
  input  IR2,
  input  IR3,
  input  ret,
  input  ie,
  input  in_7,
  output [1:0] IntNo,
  output LED1,
  output INT1,
  output INT2,
  output INT3,
  output LED2,
  output LED3
);

  wire and_1_out, and_2_out, and_3_out, and_7_out, clk_t, d_ff_1_q, d_ff_2_q, d_ff_3_q, IM1, IM1_q, IM2,
       IM2_q, IM3, IM3_q, im30, IR1_4_q, IR1_t, IR2_t, IR10, IR20, IR30, or_6_out, or_7_out, or_8_out,
       or_9_out, or_10_out, register_4_q, register_7_q, register_8_q, register_9_q, register_10_q, reset1,
       reset2, reset3;
  wire [1:0] priority_encoder_1_out;

  Clock clock_1 (.out(clk_t));
  Register #(.width(1)) u_IM1 (.D(IM1), .en(1'b1), .Q(IM1_q), .clk(clk_t));  // open: clr
  Register #(.width(1)) u_IM2 (.D(IM2), .en(1'b1), .Q(IM2_q), .clk(clk_t));  // open: clr
  Register #(.width(1)) u_IM3 (.D(IM3), .en(1'b1), .Q(IM3_q), .clk(clk_t));  // open: clr
  or or_1 (LED1, IR1_t, d_ff_1_q);
  or or_2 (LED2, IR2_t, d_ff_2_q);
  or or_3 (LED3, IM3, d_ff_3_q);
  D_Flip_Flop d_ff_1 (.clk(IR1), .D(1'b1), .Q(d_ff_1_q), .reset(IR1_t));  // open: Qn, preset, en
  D_Flip_Flop d_ff_2 (.clk(IR2), .D(1'b1), .Q(d_ff_2_q), .reset(IR2_t));  // open: Qn, preset, en
  D_Flip_Flop d_ff_3 (.clk(IR3), .D(1'b1), .Q(d_ff_3_q), .reset(IM3));  // open: Qn, preset, en
  or or_4 (IM1, IR1_t, IR2_t, IM3);
  or or_5 (IM2, IR2_t, IM3);
  or or_6 (or_6_out, d_ff_1_q, IR1_t);
  or or_7 (or_7_out, d_ff_2_q, IR2_t);
  or or_8 (or_8_out, d_ff_3_q, IM3);
  buf and_1 (and_1_out, or_6_out);  // AND_Gate AND_Gate
  buf and_2 (and_2_out, or_7_out);  // AND_Gate AND_Gate
  buf and_3 (and_3_out, or_8_out);  // AND_Gate AND_Gate
  D_Flip_Flop u_IR1 (.clk(clk_t), .D(and_1_out), .Q(IR1_t), .reset(reset1));  // open: Qn, preset, en
  D_Flip_Flop IR1_2 (.clk(clk_t), .D(and_2_out), .Q(IR2_t), .reset(reset2));  // open: Qn, preset, en
  D_Flip_Flop IR1_3 (.clk(clk_t), .D(and_3_out), .Q(IM3), .reset(reset3));  // open: Qn, preset, en
  Register #(.width(1)) register_1 (.D(reset3), .Q(im30), .clk(clk_t));  // open: en, clr
  and and_4 (IR10, IR1_t, ~IM1_q);  // AND_Gate
  and and_5 (IR20, IR2_t, ~IM2_q);  // AND_Gate
  and and_6 (IR30, IM3, ~IM3_q);  // AND_Gate
  Demultiplexer #(.select(2), .enable("false")) demultiplexer_1 (
    .out1(reset1), .out2(reset2), .out3(reset3), .in(ret), .sel(IntNo));  // open: out0
  or or_9 (or_9_out, IR10, IR20, IR30);
  and and_7 (and_7_out, or_9_out, ie);
  Priority_Encoder #(.select(2)) priority_encoder_1 (
    .in0(1'b0), .in1(IR1_t), .in2(IR2_t), .in3(IM3), .out(priority_encoder_1_out), .en_in(ie));  // open: gs, en_out
  Register #(.width(1)) register_2 (.D(and_7_out), .Q(INT1), .clk(clk_t), .clr(register_4_q));  // open: en
  Register #(.width(2)) register_3 (.D(priority_encoder_1_out), .Q(IntNo), .clk(clk_t), .clr(or_10_out));  // open: en
  or or_10 (or_10_out, ~ie, ret);  // OR_Gate
  Register #(.width(1)) register_4 (.D(1'b1), .en(INT1), .Q(register_4_q), .clk(clk_t), .clr(ie));
  // Probe on IntNo
  Register #(.width(1)) register_5 (.D(INT1), .Q(INT2), .clk(clk_t), .clr(register_7_q));  // open: en
  Register #(.width(1)) register_6 (.D(INT2), .Q(INT3), .clk(clk_t), .clr(register_8_q));  // open: en
  Register #(.width(1)) register_7 (.D(1'b1), .en(INT2), .Q(register_7_q), .clk(clk_t), .clr(ie));
  D_Flip_Flop IR1_4 (.clk(clk_t), .D(in_7), .Q(IR1_4_q), .en(reset1));  // open: Qn, preset, reset
  Register #(.width(1)) register_8 (.D(1'b1), .en(INT3), .Q(register_8_q), .clk(clk_t), .clr(ie));
  Register #(.width(1)) register_9 (.D(INT3), .Q(register_9_q), .clk(clk_t), .clr(register_10_q));  // open: en
  Register #(.width(1)) register_10 (.D(1'b1), .en(register_9_q), .Q(register_10_q), .clk(clk_t), .clr(ie));

  // Other names for the same wires on the sheet: IR3_t = IM3

  // Notes on the sheet:
  //   Reset 
  //   Reset 
  //   Reset 
endmodule

module cp0 (
  input  op5,
  input  op4,
  input  op3,
  input  op2,
  input  op1,
  input  op0,
  input  m4,
  input  m3,
  input  m2,
  input  m1,
  input  m0,
  output eret,
  output mfc0,
  output mtc0
);

  wire not_1_out, not_2_out, not_3_out, not_4_out, not_5_out, not_6_out, not_7_out, not_8_out, not_9_out,
       not_10_out, not_11_out, not_12_out, not_13_out, not_14_out, not_15_out, not_16_out, not_17_out,
       not_18_out, not_19_out, not_20_out, not_21_out, not_22_out, not_23_out, not_24_out, not_25_out,
       not_26_out, not_27_out, not_28_out;

  not not_1 (not_1_out, op5);
  not not_2 (not_2_out, op3);
  not not_3 (not_3_out, op2);
  not not_4 (not_4_out, op1);
  not not_5 (not_5_out, op0);
  not not_6 (not_6_out, m3);
  not not_7 (not_7_out, m2);
  not not_8 (not_8_out, m1);
  not not_9 (not_9_out, m0);
  not not_10 (not_10_out, op5);
  not not_11 (not_11_out, op3);
  not not_12 (not_12_out, op2);
  not not_13 (not_13_out, op1);
  not not_14 (not_14_out, op0);
  not not_15 (not_15_out, m4);
  not not_16 (not_16_out, m3);
  not not_17 (not_17_out, m2);
  not not_18 (not_18_out, m1);
  not not_19 (not_19_out, m0);
  not not_20 (not_20_out, op5);
  not not_21 (not_21_out, op3);
  not not_22 (not_22_out, op2);
  not not_23 (not_23_out, op1);
  not not_24 (not_24_out, op0);
  not not_25 (not_25_out, m4);
  not not_26 (not_26_out, m3);
  not not_27 (not_27_out, m1);
  not not_28 (not_28_out, m0);
  and and_1 (eret, not_1_out, op4, not_2_out, not_3_out, not_4_out, not_5_out, m4, not_6_out, not_7_out, not_8_out, not_9_out);
  and and_2 (mfc0, not_10_out, op4, not_11_out, not_12_out, not_13_out, not_14_out, not_15_out, not_16_out, not_17_out, not_18_out, not_19_out);
  and and_3 (mtc0, not_20_out, op4, not_21_out, not_22_out, not_23_out, not_24_out, not_25_out, not_26_out, m2, not_27_out, not_28_out);
endmodule

module it (
  input  clk,
  input  \int ,
  input  \同步清零信号 ,
  output \与中断屏蔽位与 
);

  wire and_1_out, d_ff_1_q, or_1_out, or_2_out;

  LED \_1号中断等待指示灯  (.in(or_1_out));
  or or_1 (or_1_out, \与中断屏蔽位与 , d_ff_1_q);
  D_Flip_Flop d_ff_1 (.clk(\int ), .D(1'b1), .Q(d_ff_1_q), .reset(\与中断屏蔽位与 ));  // open: Qn, preset, en
  or or_2 (or_2_out, d_ff_1_q, \与中断屏蔽位与 );
  and and_1 (and_1_out, or_2_out, ~\同步清零信号 );  // AND_Gate
  D_Flip_Flop IR1 (.clk(clk), .D(and_1_out), .Q(\与中断屏蔽位与 ));  // open: Qn, preset, en, reset

  // Notes on the sheet:
  //   Reset 
endmodule

module instruction (
  input  [9:0] instructionin,
  input  enable,
  input  [1:0] iterNo,
  output [31:0] instructionout
);

  wire demultiplexer_1_out0, demultiplexer_1_out1, demultiplexer_1_out2, demultiplexer_1_out3;
  wire [31:0] rom_1_data, rom_2_data, rom_3_data, rom_4_data;

  Demultiplexer #(.select(2), .enable("false")) demultiplexer_1 (
    .out0(demultiplexer_1_out0), .out1(demultiplexer_1_out1), .out2(demultiplexer_1_out2),
    .out3(demultiplexer_1_out3), .in(enable), .sel(iterNo));
  ROM #(.addrWidth(10), .dataWidth(32)) rom_1 (.addr(instructionin), .data(rom_1_data), .sel(demultiplexer_1_out0));
  ROM #(.addrWidth(10), .dataWidth(32)) rom_2 (.addr(instructionin), .data(rom_2_data), .sel(demultiplexer_1_out1));
  ROM #(.addrWidth(10), .dataWidth(32)) rom_3 (.addr(instructionin), .data(rom_3_data), .sel(demultiplexer_1_out2));
  ROM #(.addrWidth(10), .dataWidth(32)) rom_4 (.addr(instructionin), .data(rom_4_data), .sel(demultiplexer_1_out3));
  Multiplexer #(.select(2), .width(32), .enable("false")) multiplexer_1 (
    .in0(rom_1_data), .in1(rom_2_data), .in2(rom_3_data), .in3(rom_4_data), .out(instructionout), .sel(iterNo));

  // Notes on the sheet:
  //   contents of rom_1 (hex, n*v repeats v):
  //   20110004 ae310000 8e320000 2252fffc 20100000 22110001 2118020 22520004 ae500000 22310001 2118020
  //   22520004 ae500000 22310001 2118020 22520004 ae500000 22310001 2118020 22520004 ae500000 22310001
  //   2118020 22520004 ae500000 22310001 2118020 22520004 ae500000 22310001 2118020 22520004 ae500000
  //   2002000a 20100000 20100000 20100000 c
endmodule

module IF_ID (
  input  clear,
  input  nop,
  input  [31:0] pc_next,
  input  [31:0] pc,
  input  clk,
  output [31:0] out_6,
  output [31:0] out_7
);

  wire not_1_out;
  wire [31:0] multiplexer_1_out, multiplexer_2_out;

  not not_1 (not_1_out, nop);
  Multiplexer #(.width(32), .enable("false")) multiplexer_1 (
    .in0(pc_next), .in1({32{1'b0}}), .out(multiplexer_1_out), .sel(clear));
  Multiplexer #(.width(32), .enable("false")) multiplexer_2 (
    .in0(pc), .in1({32{1'b0}}), .out(multiplexer_2_out), .sel(clear));
  Register #(.width(32)) register_1 (.D(multiplexer_1_out), .en(not_1_out), .Q(out_6), .clk(clk));  // open: clr
  Register #(.width(32)) register_2 (.D(multiplexer_2_out), .en(not_1_out), .Q(out_7), .clk(clk));  // open: clr
endmodule

module ID_EX (
  input  clear,
  input  nop,
  input  clk,
  input  [31:0] signal,
  input  [31:0] pc,
  input  [31:0] R1,
  input  [31:0] R2,
  input  [4:0] writereg_num,
  input  [31:0] in_9,
  input  [31:0] in_10,
  input  [27:0] in_11,
  input  [31:0] in_12,
  input  [31:0] in_13,
  output [31:0] out_14,
  output [31:0] out_15,
  output [31:0] out_16,
  output [31:0] out_17,
  output [4:0] out_18,
  output [31:0] out_19,
  output [31:0] out_20,
  output [27:0] out_21,
  output [31:0] out_22,
  output [31:0] out_23
);

  wire not_1_out;
  wire [4:0] multiplexer_5_out;
  wire [27:0] multiplexer_8_out;
  wire [31:0] multiplexer_1_out, multiplexer_2_out, multiplexer_3_out, multiplexer_4_out, multiplexer_6_out,
       multiplexer_7_out, multiplexer_9_out, multiplexer_10_out;

  Multiplexer #(.width(32), .enable("false")) multiplexer_1 (
    .in0(signal), .in1({32{1'b0}}), .out(multiplexer_1_out), .sel(clear));
  Multiplexer #(.width(32), .enable("false")) multiplexer_2 (
    .in0(pc), .in1({32{1'b0}}), .out(multiplexer_2_out), .sel(clear));
  Multiplexer #(.width(32), .enable("false")) multiplexer_3 (
    .in0(R1), .in1({32{1'b0}}), .out(multiplexer_3_out), .sel(clear));
  Multiplexer #(.width(32), .enable("false")) multiplexer_4 (
    .in0(R2), .in1({32{1'b0}}), .out(multiplexer_4_out), .sel(clear));
  Multiplexer #(.width(5), .enable("false")) multiplexer_5 (
    .in0(writereg_num), .in1({5{1'b0}}), .out(multiplexer_5_out), .sel(clear));
  Multiplexer #(.width(32), .enable("false")) multiplexer_6 (
    .in0(in_9), .in1({32{1'b0}}), .out(multiplexer_6_out), .sel(clear));
  Multiplexer #(.width(32), .enable("false")) multiplexer_7 (
    .in0(in_10), .in1({32{1'b0}}), .out(multiplexer_7_out), .sel(clear));
  Multiplexer #(.width(28), .enable("false")) multiplexer_8 (
    .in0(in_11), .in1({28{1'b0}}), .out(multiplexer_8_out), .sel(clear));
  Multiplexer #(.width(32), .enable("false")) multiplexer_9 (
    .in0(in_12), .in1({32{1'b0}}), .out(multiplexer_9_out), .sel(clear));
  Multiplexer #(.width(32), .enable("false")) multiplexer_10 (
    .in0(in_13), .in1({32{1'b0}}), .out(multiplexer_10_out), .sel(clear));
  not not_1 (not_1_out, nop);
  Register #(.width(32)) register_1 (.D(multiplexer_1_out), .en(not_1_out), .Q(out_14), .clk(clk));  // open: clr
  Register #(.width(32)) register_2 (.D(multiplexer_2_out), .en(not_1_out), .Q(out_15), .clk(clk));  // open: clr
  Register #(.width(32)) register_3 (.D(multiplexer_3_out), .en(not_1_out), .Q(out_16), .clk(clk));  // open: clr
  Register #(.width(32)) register_4 (.D(multiplexer_4_out), .en(not_1_out), .Q(out_17), .clk(clk));  // open: clr
  Register #(.width(5)) register_5 (.D(multiplexer_5_out), .en(not_1_out), .Q(out_18), .clk(clk));  // open: clr
  Register #(.width(32)) register_6 (.D(multiplexer_6_out), .en(not_1_out), .Q(out_19), .clk(clk));  // open: clr
  Register #(.width(32)) register_7 (.D(multiplexer_7_out), .en(not_1_out), .Q(out_20), .clk(clk));  // open: clr
  Register #(.width(28)) register_8 (.D(multiplexer_8_out), .en(not_1_out), .Q(out_21), .clk(clk));  // open: clr
  Register #(.width(32)) register_9 (.D(multiplexer_9_out), .en(not_1_out), .Q(out_22), .clk(clk));  // open: clr
  Register #(.width(32)) register_10 (.D(multiplexer_10_out), .en(not_1_out), .Q(out_23), .clk(clk));  // open: clr
endmodule

module EX_MEM (
  input  nop,
  input  clk,
  input  clear,
  input  [31:0] in_4,
  input  [31:0] signal,
  input  [31:0] pc,
  input  [31:0] R1,
  input  [31:0] R2,
  input  [31:0] writeback,
  input  [31:0] in_10,
  input  [31:0] in_11,
  input  in_12,
  input  [27:0] in_13,
  input  [31:0] in_14,
  input  [4:0] in_15,
  output [31:0] out_16,
  output [31:0] out_17,
  output [31:0] out_18,
  output [31:0] out_19,
  output [31:0] out_20,
  output [31:0] out_21,
  output [31:0] out_22,
  output [31:0] out_23,
  output out_24,
  output [27:0] out_25,
  output [31:0] out_26,
  output [4:0] out_27
);

  wire not_1_out;

  not not_1 (not_1_out, nop);
  Register #(.width(32)) register_1 (.D(in_4), .en(not_1_out), .Q(out_16), .clk(clk), .clr(clear));
  Register #(.width(32)) register_2 (.D(signal), .en(not_1_out), .Q(out_17), .clk(clk), .clr(clear));
  Register #(.width(32)) register_3 (.D(pc), .en(not_1_out), .Q(out_18), .clk(clk), .clr(clear));
  Register #(.width(32)) register_4 (.D(R1), .en(not_1_out), .Q(out_19), .clk(clk), .clr(clear));
  Register #(.width(32)) register_5 (.D(R2), .en(not_1_out), .Q(out_20), .clk(clk), .clr(clear));
  Register #(.width(32)) register_6 (.D(writeback), .en(not_1_out), .Q(out_21), .clk(clk), .clr(clear));
  Register #(.width(32)) register_7 (.D(in_10), .en(not_1_out), .Q(out_22), .clk(clk), .clr(clear));
  Register #(.width(32)) register_8 (.D(in_11), .en(not_1_out), .Q(out_23), .clk(clk), .clr(clear));
  Register #(.width(1)) register_9 (.D(in_12), .en(not_1_out), .Q(out_24), .clk(clk), .clr(clear));
  Register #(.width(28)) register_10 (.D(in_13), .en(not_1_out), .Q(out_25), .clk(clk), .clr(clear));
  Register #(.width(32)) register_11 (.D(in_14), .en(not_1_out), .Q(out_26), .clk(clk), .clr(clear));
  Register #(.width(5)) register_12 (.D(in_15), .en(not_1_out), .Q(out_27), .clk(clk), .clr(clear));
endmodule

module MEM_WB (
  input  clear,
  input  nop,
  input  clk,
  input  [31:0] in_4,
  input  [31:0] in_5,
  input  [31:0] in_6,
  input  in_7,
  input  in_8,
  input  [4:0] in_9,
  input  [31:0] in_10,
  input  in_11,
  input  in_12,
  input  in_13,
  output [31:0] out_14,
  output [31:0] out_15,
  output [31:0] out_16,
  output out_17,
  output out_18,
  output [4:0] out_19,
  output [31:0] out_20,
  output out_21,
  output out_22,
  output out_23
);

  wire not_1_out;

  not not_1 (not_1_out, nop);
  Register #(.width(32)) register_1 (.D(in_4), .en(not_1_out), .Q(out_14), .clk(clk), .clr(clear));
  Register #(.width(32)) register_2 (.D(in_5), .en(not_1_out), .Q(out_15), .clk(clk), .clr(clear));
  Register #(.width(32)) register_3 (.D(in_6), .en(not_1_out), .Q(out_16), .clk(clk), .clr(clear));
  Register #(.width(1)) register_4 (.D(in_7), .en(not_1_out), .Q(out_17), .clk(clk), .clr(clear));
  Register #(.width(1)) register_5 (.D(in_8), .en(not_1_out), .Q(out_18), .clk(clk), .clr(clear));
  Register #(.width(5)) register_6 (.D(in_9), .en(not_1_out), .Q(out_19), .clk(clk), .clr(clear));
  Register #(.width(32)) register_7 (.D(in_10), .en(not_1_out), .Q(out_20), .clk(clk), .clr(clear));
  Register #(.width(1)) register_8 (.D(in_11), .en(not_1_out), .Q(out_21), .clk(clk), .clr(clear));
  Register #(.width(1)) register_9 (.D(in_12), .en(not_1_out), .Q(out_22), .clk(clk), .clr(clear));
  Register #(.width(1)) register_10 (.D(in_13), .en(not_1_out), .Q(out_23), .clk(clk), .clr(clear));
endmodule

module pop (
  input  [4:0] RT,
  input  [4:0] RW_EX,
  input  RegWrite_EX,
  input  [4:0] RW_MEM,
  input  RegWrite_MEM,
  input  [4:0] RW_WB,
  input  RegWrite_WB,
  input  beq,
  input  bne,
  input  \R型指令 ,
  input  [4:0] RS,
  input  jr,
  input  lui,
  input  ALUsrc,
  input  shift,
  input  bgtz,
  input  SysCall,
  output nop
);

  wire and_1_out, and_2_out, and_3_out, and_4_out, and_5_out, and_6_out, and_7_out, and_8_out, and_9_out,
       and_10_out, and_11_out, and_12_out, and_13_out, and_14_out, and_15_out, and_16_out, and_17_out,
       and_18_out, and_19_out, comparator_1_eq, comparator_2_eq, comparator_3_eq, comparator_4_eq,
       comparator_5_eq, comparator_6_eq, comparator_7_eq, comparator_8_eq, comparator_9_eq, comparator_10_eq,
       comparator_11_eq, comparator_12_eq, comparator_13_eq, comparator_14_eq, comparator_15_eq, or_2_out,
       or_3_out, or_4_out, or_5_out, ppp;

  Comparator #(.width(5)) comparator_1 (.a({5{1'b0}}), .b(RW_EX), .eq(comparator_1_eq));  // open: gt, lt
  Comparator #(.width(5)) comparator_2 (.a({5{1'b0}}), .b(RW_MEM), .eq(comparator_2_eq));  // open: gt, lt
  Comparator #(.width(5)) comparator_3 (.a({5{1'b0}}), .b(RW_WB), .eq(comparator_3_eq));  // open: gt, lt
  and and_1 (and_1_out, ~comparator_1_eq, RegWrite_EX);  // AND_Gate
  and and_2 (and_2_out, ~comparator_2_eq, RegWrite_MEM);  // AND_Gate
  and and_3 (and_3_out, ~comparator_3_eq, RegWrite_WB);  // AND_Gate
  Comparator #(.width(5)) comparator_4 (.a({5{1'b0}}), .b(RW_EX), .eq(comparator_4_eq));  // open: gt, lt
  and and_4 (and_4_out, ~comparator_4_eq, RegWrite_EX);  // AND_Gate
  Comparator #(.width(5)) comparator_5 (.a({5{1'b0}}), .b(RW_MEM), .eq(comparator_5_eq));  // open: gt, lt
  and and_5 (and_5_out, ~comparator_5_eq, RegWrite_MEM);  // AND_Gate
  Comparator #(.width(5)) comparator_6 (.a({5{1'b0}}), .b(RW_WB), .eq(comparator_6_eq));  // open: gt, lt
  and and_6 (and_6_out, ~comparator_6_eq, RegWrite_WB);  // AND_Gate
  Comparator #(.width(5)) comparator_7 (.a(5'b00010), .b(RW_EX), .eq(comparator_7_eq));  // open: gt, lt
  Comparator #(.width(5)) comparator_8 (.a(5'b00010), .b(RW_MEM), .eq(comparator_8_eq));  // open: gt, lt
  Comparator #(.width(5)) comparator_9 (.a(5'b00010), .b(RW_WB), .eq(comparator_9_eq));  // open: gt, lt
  Comparator #(.width(5)) comparator_10 (.a(RT), .b(RW_EX), .eq(comparator_10_eq));  // open: gt, lt
  Comparator #(.width(5)) comparator_11 (.a(RT), .b(RW_MEM), .eq(comparator_11_eq));  // open: gt, lt
  Comparator #(.width(5)) comparator_12 (.a(RT), .b(RW_WB), .eq(comparator_12_eq));  // open: gt, lt
  and and_7 (and_7_out, \R型指令 , ~SysCall);  // AND_Gate
  Comparator #(.width(5)) comparator_13 (.a(RS), .b(RW_EX), .eq(comparator_13_eq));  // open: gt, lt
  Comparator #(.width(5)) comparator_14 (.a(RS), .b(RW_MEM), .eq(comparator_14_eq));  // open: gt, lt
  Comparator #(.width(5)) comparator_15 (.a(RS), .b(RW_WB), .eq(comparator_15_eq));  // open: gt, lt
  and and_8 (and_8_out, RegWrite_EX, comparator_7_eq);
  and and_9 (and_9_out, RegWrite_MEM, comparator_8_eq);
  and and_10 (and_10_out, RegWrite_WB, comparator_9_eq);
  and and_11 (and_11_out, and_1_out, comparator_10_eq);
  and and_12 (and_12_out, and_2_out, comparator_11_eq);
  and and_13 (and_13_out, and_3_out, comparator_12_eq);
  or or_1 (ppp, beq, bne, and_7_out);
  and and_14 (and_14_out, and_4_out, comparator_13_eq);
  and and_15 (and_15_out, and_5_out, comparator_14_eq);
  and and_16 (and_16_out, and_6_out, comparator_15_eq);
  or or_2 (or_2_out, and_8_out, and_9_out, and_10_out);
  or or_3 (or_3_out, and_11_out, and_12_out, and_13_out);
  or or_4 (or_4_out, and_14_out, and_15_out, and_16_out);
  or or_5 (or_5_out, ppp, jr, lui, ALUsrc, shift, bgtz, SysCall);
  and and_17 (and_17_out, or_3_out, ppp);
  and and_18 (and_18_out, or_4_out, or_5_out);
  and and_19 (and_19_out, or_2_out, SysCall);
  or or_6 (nop, and_17_out, and_18_out, and_19_out);
endmodule

module redirection (
  input  [4:0] writereg0,
  input  [4:0] rs,
  input  [4:0] rt,
  input  shift,
  input  ALUsrc,
  input  Regwrite,
  input  MemtoReg,
  input  [4:0] writereg1,
  input  Regwrite3,
  output from1R1,
  output nop,
  output from1Y,
  output from1R2,
  output from2R1,
  output from2Y,
  output from2R2
);

  wire and_1_out, and_2_out, and_4_out, and_5_out, and_7_out, and_8_out, and_11_out, and_13_out, and_14_out,
       comparator_1_eq, comparator_2_eq, comparator_3_eq, comparator_4_eq, comparator_5_eq, comparator_6_eq,
       comparator_7_eq, comparator_8_eq, comparator_9_eq, comparator_10_eq, comparator_11_eq,
       comparator_12_eq, not_1_out, not_2_out, not_3_out, not_4_out, not_5_out, not_6_out, not_7_out,
       not_8_out, not_9_out, not_10_out, not_11_out, not_12_out, not_13_out, or_1_out, or_2_out, or_3_out;
  wire [4:0] multiplexer_1_out, multiplexer_2_out, multiplexer_3_out, multiplexer_4_out;

  not not_1 (not_1_out, shift);
  not not_2 (not_2_out, ALUsrc);
  not not_3 (not_3_out, shift);
  not not_4 (not_4_out, ALUsrc);
  Comparator #(.width(5)) comparator_1 (.a(writereg0), .b({5{1'b0}}), .eq(comparator_1_eq));  // open: gt, lt
  Comparator #(.width(5)) comparator_2 (.a(rs), .b({5{1'b0}}), .eq(comparator_2_eq));  // open: gt, lt
  Comparator #(.width(5)) comparator_3 (.a(rt), .b({5{1'b0}}), .eq(comparator_3_eq));  // open: gt, lt
  Multiplexer #(.width(5), .enable("false")) multiplexer_1 (
    .in0({5{1'b0}}), .in1(rs), .out(multiplexer_1_out), .sel(not_1_out));
  Multiplexer #(.width(5), .enable("false")) multiplexer_2 (
    .in0({5{1'b0}}), .in1(rt), .out(multiplexer_2_out), .sel(or_1_out));
  or or_1 (or_1_out, shift, not_2_out);
  Comparator #(.width(5)) comparator_4 (.a(writereg1), .b({5{1'b0}}), .eq(comparator_4_eq));  // open: gt, lt
  Comparator #(.width(5)) comparator_5 (.a(rs), .b({5{1'b0}}), .eq(comparator_5_eq));  // open: gt, lt
  Comparator #(.width(5)) comparator_6 (.a(rt), .b({5{1'b0}}), .eq(comparator_6_eq));  // open: gt, lt
  Multiplexer #(.width(5), .enable("false")) multiplexer_3 (
    .in0({5{1'b0}}), .in1(rs), .out(multiplexer_3_out), .sel(not_3_out));
  Multiplexer #(.width(5), .enable("false")) multiplexer_4 (
    .in0({5{1'b0}}), .in1(rt), .out(multiplexer_4_out), .sel(or_2_out));
  or or_2 (or_2_out, shift, not_4_out);
  not not_5 (not_5_out, comparator_1_eq);
  not not_6 (not_6_out, comparator_2_eq);
  not not_7 (not_7_out, comparator_3_eq);
  Comparator #(.width(5)) comparator_7 (.a(writereg0), .b(multiplexer_1_out), .eq(comparator_7_eq));  // open: gt, lt
  Comparator #(.width(5)) comparator_8 (.a(writereg0), .b(multiplexer_2_out), .eq(comparator_8_eq));  // open: gt, lt
  Comparator #(.width(5)) comparator_9 (.a(writereg0), .b(rt), .eq(comparator_9_eq));  // open: gt, lt
  not not_8 (not_8_out, comparator_4_eq);
  not not_9 (not_9_out, comparator_5_eq);
  not not_10 (not_10_out, comparator_6_eq);
  Comparator #(.width(5)) comparator_10 (.a(writereg1), .b(multiplexer_3_out), .eq(comparator_10_eq));  // open: gt, lt
  Comparator #(.width(5)) comparator_11 (.a(writereg1), .b(multiplexer_4_out), .eq(comparator_11_eq));  // open: gt, lt
  Comparator #(.width(5)) comparator_12 (.a(writereg1), .b(rt), .eq(comparator_12_eq));  // open: gt, lt
  and and_1 (and_1_out, not_5_out, not_6_out, comparator_7_eq);
  and and_2 (and_2_out, not_5_out, comparator_8_eq, not_7_out);
  and and_3 (from1R2, not_5_out, not_7_out, comparator_9_eq, ALUsrc);
  and and_4 (and_4_out, not_8_out, not_9_out, comparator_10_eq);
  and and_5 (and_5_out, not_8_out, comparator_11_eq, not_10_out);
  and and_6 (from2R2, not_8_out, not_10_out, comparator_12_eq, ALUsrc);
  and and_7 (and_7_out, and_1_out, MemtoReg);
  not not_11 (not_11_out, MemtoReg);
  not not_12 (not_12_out, MemtoReg);
  and and_8 (and_8_out, MemtoReg, and_2_out);
  and and_9 (from2R1, and_4_out, Regwrite3);
  and and_10 (from2Y, Regwrite3, and_5_out);
  or or_3 (or_3_out, and_7_out, and_8_out);
  and and_11 (and_11_out, and_1_out, not_11_out, Regwrite);
  and and_12 (nop, or_3_out, Regwrite);
  and and_13 (and_13_out, not_12_out, and_2_out, Regwrite);
  and and_14 (and_14_out, shift, and_13_out);
  or or_4 (from1R1, and_11_out, and_14_out);
  not not_13 (not_13_out, and_14_out);
  and and_15 (from1Y, not_13_out, and_13_out);

  // Other names for the same wires on the sheet: R1[4:0] = rs; R2[4:0] = rt
endmodule
