// Logisim project regfile.circ as structural Verilog: 1 circuit, main circuit main
module main (
  input  [4:0] Reg1_num,
  input  [4:0] Reg2,
  input  [4:0] Write_Reg_num,
  input  [31:0] Din,
  input  Write_Enable,
  input  Clock,
  input  in_7,
  output [31:0] Reg1,
  output [31:0] s0_Value,
  output [31:0] s1_Value,
  output [31:0] s2_Value,
  output [31:0] ra_Value,
  output [31:0] Reg2_2
);

  wire _1i, _2i, _3i, _4i, _5i, _6i, _7i, _8i, _9i, _10i, _11i, _12i, _13i, _14i, _15i, _16i, _17i, _18i,
       _19i, _20i, _21i, _22i, _23i, _24i, _25i, _26i, _27i, _28i, _29i, _30i, _31i;
  wire [31:0] _0o, _1o, _3o, _5o, _6o, _7o, _8o, _9o, _10o, _11o, _12o, _13o, _14o, _15o, _16o, _19o, _20o,
       _21o, _22o, _23o, _24o, _25o, _26o, _27o, _28o, _29o, _30o, _31o;

  Demultiplexer #(.select(5), .disabled(0), .enable("false")) demultiplexer_1 (
    .out1(_1i), .out2(_2i), .out3(_3i), .out4(_4i), .out5(_5i), .out6(_6i), .out7(_7i), .out8(_8i),
    .out9(_9i), .out10(_10i), .out11(_11i), .out12(_12i), .out13(_13i), .out14(_14i), .out15(_15i),
    .out16(_16i), .out17(_17i), .out18(_18i), .out19(_19i), .out20(_20i), .out21(_21i), .out22(_22i),
    .out23(_23i), .out24(_24i), .out25(_25i), .out26(_26i), .out27(_27i), .out28(_28i), .out29(_29i),
    .out30(_30i), .out31(_31i), .in(Write_Enable), .sel(Write_Reg_num));  // open: out0
  Register #(.width(32)) reg0 (.D(Din), .en(in_7), .Q(_0o), .clk(Clock), .clr(1'b1));
  Register #(.width(32)) reg8 (.D(Din), .en(_8i), .Q(_8o), .clk(Clock), .clr(1'b0));
  Register #(.width(32)) reg16 (.D(Din), .en(_16i), .Q(_16o), .clk(Clock), .clr(1'b0));
  Register #(.width(32)) reg24 (.D(Din), .en(_24i), .Q(_24o), .clk(Clock), .clr(1'b0));
  Register #(.width(32)) u_reg1 (.D(Din), .en(_1i), .Q(_1o), .clk(Clock), .clr(1'b0));
  Register #(.width(32)) reg9 (.D(Din), .en(_9i), .Q(_9o), .clk(Clock), .clr(1'b0));
  Register #(.width(32)) reg17 (.D(Din), .en(_17i), .Q(s1_Value), .clk(Clock), .clr(1'b0));
  Register #(.width(32)) reg25 (.D(Din), .en(_25i), .Q(_25o), .clk(Clock), .clr(1'b0));
  Register #(.width(32)) u_reg2 (.D(Din), .en(_2i), .Q(s0_Value), .clk(Clock), .clr(1'b0));
  Register #(.width(32)) reg10 (.D(Din), .en(_10i), .Q(_10o), .clk(Clock), .clr(1'b0));
  Register #(.width(32)) reg18 (.D(Din), .en(_18i), .Q(s2_Value), .clk(Clock), .clr(1'b0));
  Register #(.width(32)) reg26 (.D(Din), .en(_26i), .Q(_26o), .clk(Clock), .clr(1'b0));
  Register #(.width(32)) reg3 (.D(Din), .en(_3i), .Q(_3o), .clk(Clock), .clr(1'b0));
  Register #(.width(32)) reg11 (.D(Din), .en(_11i), .Q(_11o), .clk(Clock), .clr(1'b0));
  Register #(.width(32)) reg19 (.D(Din), .en(_19i), .Q(_19o), .clk(Clock), .clr(1'b0));
  Register #(.width(32)) reg27 (.D(Din), .en(_27i), .Q(_27o), .clk(Clock), .clr(1'b0));
  Register #(.width(32)) reg4 (.D(Din), .en(_4i), .Q(ra_Value), .clk(Clock), .clr(1'b0));
  Register #(.width(32)) reg12 (.D(Din), .en(_12i), .Q(_12o), .clk(Clock), .clr(1'b0));
  Register #(.width(32)) reg20 (.D(Din), .en(_20i), .Q(_20o), .clk(Clock), .clr(1'b0));
  Register #(.width(32)) reg28 (.D(Din), .en(_28i), .Q(_28o), .clk(Clock), .clr(1'b0));
  Multiplexer #(.select(5), .width(32), .disabled(0), .enable("false")) multiplexer_1 (
    .in0(_0o), .in1(_1o), .in2(s0_Value), .in3(_3o), .in4(ra_Value), .in5(_5o), .in6(_6o), .in7(_7o),
    .in8(_8o), .in9(_9o), .in10(_10o), .in11(_11o), .in12(_12o), .in13(_13o), .in14(_14o), .in15(_15o),
    .in16(_16o), .in17(s1_Value), .in18(s2_Value), .in19(_19o), .in20(_20o), .in21(_21o), .in22(_22o),
    .in23(_23o), .in24(_24o), .in25(_25o), .in26(_26o), .in27(_27o), .in28(_28o), .in29(_29o), .in30(_30o),
    .in31(_31o), .out(Reg1), .sel(Reg1_num));
  Register #(.width(32)) reg5 (.D(Din), .en(_5i), .Q(_5o), .clk(Clock), .clr(1'b0));
  Register #(.width(32)) reg13 (.D(Din), .en(_13i), .Q(_13o), .clk(Clock), .clr(1'b0));
  Register #(.width(32)) reg21 (.D(Din), .en(_21i), .Q(_21o), .clk(Clock), .clr(1'b0));
  Register #(.width(32)) reg29 (.D(Din), .en(_29i), .Q(_29o), .clk(Clock), .clr(1'b0));
  Register #(.width(32)) reg6 (.D(Din), .en(_6i), .Q(_6o), .clk(Clock), .clr(1'b0));
  Register #(.width(32)) reg14 (.D(Din), .en(_14i), .Q(_14o), .clk(Clock), .clr(1'b0));
  Register #(.width(32)) reg22 (.D(Din), .en(_22i), .Q(_22o), .clk(Clock), .clr(1'b0));
  Register #(.width(32)) reg30 (.D(Din), .en(_30i), .Q(_30o), .clk(Clock), .clr(1'b0));
  Register #(.width(32)) reg7 (.D(Din), .en(_7i), .Q(_7o), .clk(Clock), .clr(1'b0));
  Register #(.width(32)) reg15 (.D(Din), .en(_15i), .Q(_15o), .clk(Clock), .clr(1'b0));
  Register #(.width(32)) reg23 (.D(Din), .en(_23i), .Q(_23o), .clk(Clock), .clr(1'b0));
  Register #(.width(32)) reg31 (.D(Din), .en(_31i), .Q(_31o), .clk(Clock), .clr(1'b0));
  Multiplexer #(.select(5), .width(32), .disabled(0), .enable("false")) multiplexer_2 (
    .in0(_0o), .in1(_1o), .in2(s0_Value), .in3(_3o), .in4(ra_Value), .in5(_5o), .in6(_6o), .in7(_7o),
    .in8(_8o), .in9(_9o), .in10(_10o), .in11(_11o), .in12(_12o), .in13(_13o), .in14(_14o), .in15(_15o),
    .in16(_16o), .in17(s1_Value), .in18(s2_Value), .in19(_19o), .in20(_20o), .in21(_21o), .in22(_22o),
    .in23(_23o), .in24(_24o), .in25(_25o), .in26(_26o), .in27(_27o), .in28(_28o), .in29(_29o), .in30(_30o),
    .in31(_31o), .out(Reg2_2), .sel(Reg2));

  // Other names for the same wires on the sheet: _0i = in_7; _2o[31:0] = s0_Value; s0[31:0] = s0_Value;
  //   _4o[31:0] = ra_Value; ra[31:0] = ra_Value; _17o[31:0] = s1_Value; s1[31:0] = s1_Value; _18o[31:0] = s2_Value;
  //   s2[31:0] = s2_Value; clk = Clock; reg2_num[4:0] = Reg2; reg2_t[31:0] = Reg2_2; WE = Write_Enable;
  //   data[31:0] = Din; write_data[31:0] = Din

  // Notes on the sheet:
  //   输入引脚
  //   输出引脚
  //   Debug引脚，便于观测寄存器值
  //   请勿修改引脚以及封装，直接使用隧道连接电路
endmodule
